// Logisim project ALU Components.circ as structural Verilog: 4 circuits, main circuit Arithmatic Logic Unit
module Arithmatic_Logic_Unit (
  input  [7:0] Input_A,
  input  [7:0] Input_B,
  input  Clock,
  input  [3:0] Operation,
  input  Reset,
  output Clear_A,
  output Clear_B,
  output [3:0] Flags,
  output Set_Flags,
  output Clear_Flags,
  output Set_Output,
  output [7:0] Output
);

  wire adder_1_cout, adder_2_cout, and_5_out, comparator_1_eq, comparator_1_gt, comparator_1_lt,
       comparator_2_gt, multiplexer_2_out, nand_2_out, nand_3_out, nand_4_out, nand_5_out, nand_6_out,
       nand_7_out, nand_8_out, nand_9_out, nor_2_out, nor_3_out, nor_4_out, nor_5_out, nor_6_out, not_2_out,
       or_2_out, or_3_out, or_4_out, or_5_out, or_8_out, subtractor_1_bout, subtractor_2_bout;
  wire [7:0] adder_1_out, adder_2_out, and_1_out, multiplier_1_cout, multiplier_1_out, nand_1_out,
       negator_1_out, nor_1_out, not_1_out, or_1_out, shifter_1_out, shifter_2_out, subtractor_1_out,
       subtractor_2_out, xor_1_out;

  Adder adder_1 (.a(Input_A), .b(Input_B), .out(adder_1_out), .cout(adder_1_cout));  // open: cin
  Subtractor subtractor_1 (.a(Input_A), .b(Input_B), .out(subtractor_1_out), .bout(subtractor_1_bout));  // open: bin
  Negator negator_1 (.in(Input_A), .out(negator_1_out));
  Adder adder_2 (.a(Input_A), .b({8{1'b0}}), .out(adder_2_out), .cin(1'b1), .cout(adder_2_cout));
  Subtractor subtractor_2 (.a(Input_A), .b(8'h1), .out(subtractor_2_out), .bout(subtractor_2_bout));  // open: bin
  Multiplier multiplier_1 (.a(Input_A), .b(Input_B), .out(multiplier_1_out), .cout(multiplier_1_cout));  // open: cin
  assign not_1_out = ~Input_A;  // NOT_Gate not_1, 8 bits wide
  assign and_1_out = Input_A & Input_B;  // AND_Gate and_1, 8 bits wide
  assign nand_1_out = ~(Input_A & Input_B);  // NAND_Gate nand_1, 8 bits wide
  assign or_1_out = Input_A | Input_B;  // OR_Gate or_1, 8 bits wide
  assign nor_1_out = ~(Input_A | Input_B);  // NOR_Gate nor_1, 8 bits wide
  assign xor_1_out = Input_A ^ Input_B;  // XOR_Gate xor_1, 8 bits wide
  Shifter #(.shift("lr")) shifter_1 (.in(Input_A), .\dist (Input_B[2:0]), .out(shifter_1_out));
  Shifter shifter_2 (.in(Input_A), .\dist (Input_B[2:0]), .out(shifter_2_out));
  Comparator #(.mode("unsigned")) comparator_1 (
    .a(Input_A), .b(Input_B), .gt(comparator_1_gt), .eq(comparator_1_eq), .lt(comparator_1_lt));
  Comparator #(.mode("unsigned")) comparator_2 (.a(Input_A), .b({8{1'b0}}), .gt(comparator_2_gt));  // open: eq, lt
  or or_2 (or_2_out, comparator_1_gt, comparator_1_eq);
  or or_3 (or_3_out, comparator_1_eq, comparator_1_lt);
  not not_2 (not_2_out, nand_2_out);
  or or_4 (or_4_out, Operation[3], Operation[2], Operation[1], Operation[0]);
  nand nand_2 (nand_2_out, Operation[3], Operation[2], Operation[1], Operation[0]);
  and and_2 (Set_Output, Clock, or_4_out, nand_2_out);
  and and_3 (Flags[1], or_2_out, not_2_out);
  and and_4 (Flags[0], or_3_out, not_2_out);
  and and_5 (and_5_out, comparator_2_gt, not_2_out);
  or or_5 (or_5_out, multiplier_1_cout[0], multiplier_1_cout[1], multiplier_1_cout[2], multiplier_1_cout[3], multiplier_1_cout[4], multiplier_1_cout[5], multiplier_1_cout[6], multiplier_1_cout[7]);
  Multiplexer #(.select(4), .width(8), .disabled(0), .enable("false")) multiplexer_1 (
    .in0({8{1'b0}}), .in1(adder_1_out), .in2(subtractor_1_out), .in3(negator_1_out), .in4(adder_2_out),
    .in5(subtractor_2_out), .in6(multiplier_1_out), .in7(not_1_out), .in8(and_1_out), .in9(nand_1_out),
    .in10(or_1_out), .in11(nor_1_out), .in12(xor_1_out), .in13(shifter_1_out), .in14(shifter_2_out),
    .in15({8{1'b0}}), .out(Output), .sel(Operation));
  Multiplexer #(.select(3), .disabled(0), .enable("false")) multiplexer_2 (
    .in0(1'b0), .in1(adder_1_cout), .in2(subtractor_1_bout), .in3(1'b0), .in4(adder_2_cout),
    .in5(subtractor_2_bout), .in6(or_5_out), .in7(1'b0), .out(multiplexer_2_out), .sel(Operation[2:0]));
  nor nor_2 (nor_2_out, Operation[3], ~Operation[2], ~Operation[1], Operation[0]);  // NOR_Gate
  nor nor_3 (nor_3_out, Operation[3], ~Operation[2], Operation[1], Operation[0]);  // NOR_Gate
  nor nor_4 (nor_4_out, Operation[3], Operation[2], Operation[1], ~Operation[0]);  // NOR_Gate
  nor nor_5 (nor_5_out, Operation[3], Operation[2], ~Operation[1], Operation[0]);  // NOR_Gate
  nor nor_6 (nor_6_out, Operation[3], ~Operation[2], Operation[1], ~Operation[0]);  // NOR_Gate
  nand nand_3 (nand_3_out, multiplexer_2_out, nor_2_out);
  nand nand_4 (nand_4_out, nand_3_out, nand_5_out, nand_6_out);
  nand nand_5 (nand_5_out, multiplexer_2_out, nor_3_out);
  nand nand_6 (nand_6_out, multiplexer_2_out, nor_4_out);
  nand nand_7 (nand_7_out, multiplexer_2_out, nor_5_out);
  nand nand_8 (nand_8_out, nand_7_out, nand_9_out);
  nand nand_9 (nand_9_out, multiplexer_2_out, nor_6_out);
  or or_6 (Flags[2], nand_4_out, and_5_out);
  or or_7 (Flags[3], nand_8_out, and_5_out);
  or or_8 (or_8_out, nor_6_out, nor_5_out, nor_4_out, nor_3_out, nor_2_out, not_2_out);
  and and_6 (Set_Flags, or_8_out, Clock);

  assign Clear_A = Reset;
  assign Clear_B = Reset;
  assign Clear_Flags = Reset;
endmodule

// ALU In
module Accumulator (
  input  Set,
  input  [7:0] Data_In,
  input  Clear,
  output [7:0] Data_Out
);

  Register register_1 (.D(Data_In), .Q(Data_Out), .clk(Set), .clr(Clear));  // open: en
endmodule

// Flags
module ALU_Flags (
  input  [3:0] Flags_In,
  input  Set,
  input  Clear,
  output [3:0] Flags_Out
);

  Register #(.width(4)) register_1 (.D(Flags_In), .Q(Flags_Out), .clk(Set), .clr(Clear));  // open: en
endmodule

// OUT
module Output (
  input  Enable,
  input  [7:0] Data_In,
  input  Set,
  input  Clear,
  output [7:0] Data_Out,
  output [7:0] Print_Out
);

  Register register_1 (.D(Data_In), .Q(Print_Out), .clk(Set), .clr(Clear));  // open: en
  assign Data_Out = Enable ? Print_Out : 8'bz;  // Controlled_Buffer controlled_buffer_1
endmodule
