// Logisim project CMD Components.circ as structural Verilog: 9 circuits, main circuit Command Unit
module Command_Unit (
  input  [3:0] ALU_Flags,
  input  Reset,
  input  [7:0] Execute_Instruction,
  output ACC_Set,
  output Input_A_Set,
  output [2:0] GPR_Select,
  output GPR_Set,
  output GPR_Enable,
  output GPR_Clear,
  output Decrement_Stack,
  output Set_Stack_Address,
  output Set_Stack_Data,
  output MAR_Set,
  output MAR_Reset,
  output Load_From_Stack,
  output Load_From_IAR,
  output RAM_Set,
  output ALU_Clock,
  output DEV_Set,
  output RAM_Enable,
  output [3:0] ALU_Opcode,
  output Output_Enable,
  output IER_Reset,
  output IER_Clock,
  output IAR_Load_L,
  output IAR_Reset,
  output IAR_Load_U
);

  wire clock_1_c1, clock_1_c2, clock_1_c3, clock_1_clock, clock_1_cx, clock_1_master_enable,
       exec_alu_operation_1_gpr_enable, exec_jump_1_allow_jump, exec_move_1_gpr_enable,
       exec_move_1_master_enable_out, instruction_preprocessor_1_jmp, instruction_preprocessor_1_ld,
       instruction_preprocessor_1_ld_addr, instruction_preprocessor_1_out, instruction_processor_1_alu,
       instruction_processor_1_call, instruction_processor_1_gpr_to_acc, instruction_processor_1_gpr_to_ram,
       instruction_processor_1_jmp, instruction_processor_1_jxx, instruction_processor_1_no_operation,
       instruction_processor_1_num_to_acc, instruction_processor_1_num_to_gpr,
       instruction_processor_1_out_to_acc, instruction_processor_1_out_to_gpr,
       instruction_processor_1_out_to_ram, instruction_processor_1_ram_to_acc,
       instruction_processor_1_ram_to_gpr, instruction_processor_1_ret, mar_tasks_1_load_from_iar,
       mar_tasks_1_master_enable_out;
  wire [4:0] instruction_loader_1_clock_counter;

  and and_1 (ALU_Clock, clock_1_cx, instruction_processor_1_alu);
  Instruction_Preprocessor instruction_preprocessor_1 (
    .LD_Addr(instruction_preprocessor_1_ld_addr), .LD(instruction_preprocessor_1_ld),
    .Instruction(Execute_Instruction), .OUT(instruction_preprocessor_1_out),
    .JMP(instruction_preprocessor_1_jmp));
  Clock clock_1 (
    .Reset(Reset), .Clock(clock_1_clock), .Master_Enable(clock_1_master_enable), .C1(clock_1_c1),
    .C2(clock_1_c2), .C3(clock_1_c3), .CX(clock_1_cx));
  MAR_Tasks mar_tasks_1 (
    .Clock(clock_1_clock), .C3(clock_1_c3), .Reset(Reset), .MAR_Set(MAR_Set),
    .Master_Enable(clock_1_master_enable), .Master_Enable_Out(mar_tasks_1_master_enable_out),
    .C1(clock_1_c1), .No_Operation(instruction_processor_1_no_operation),
    .Num_To_ACC(instruction_processor_1_num_to_acc), .Out_To_RAM(instruction_processor_1_out_to_ram),
    .RAM_to_ACC(instruction_processor_1_ram_to_acc), .Out_To_ACC(instruction_processor_1_out_to_acc),
    .Unconditional_Jump(instruction_processor_1_jmp), .Conditional_Jump(instruction_processor_1_jxx),
    .Num_To_GPR(instruction_processor_1_num_to_gpr), .RAM_To_GPR(instruction_processor_1_ram_to_gpr),
    .Out_To_GPR(instruction_processor_1_out_to_gpr), .GPR_To_ACC(instruction_processor_1_gpr_to_acc),
    .GPR_To_RAM(instruction_processor_1_gpr_to_ram), .Use_ALU(instruction_processor_1_alu),
    .Clock_Counter(instruction_loader_1_clock_counter), .C2(clock_1_c2), .Load_to_Stack(Set_Stack_Data),
    .Load_From_Stack(Load_From_Stack), .Load_From_IAR(mar_tasks_1_load_from_iar),
    .CALL(instruction_processor_1_call), .RET(instruction_processor_1_ret));
  EXEC_Move exec_move_1 (
    .Clock(clock_1_clock), .C1(clock_1_c1), .C3(clock_1_c2), .CX(clock_1_cx),
    .Clock_Counter(instruction_loader_1_clock_counter), .ACC_Set(ACC_Set), .GPR_Set(GPR_Set),
    .GPR_Enable(exec_move_1_gpr_enable), .Out_Enable(Output_Enable),
    .Num_to_GPR(instruction_processor_1_num_to_gpr), .Num_to_ACC(instruction_processor_1_num_to_acc),
    .RAM_to_GPR(instruction_processor_1_ram_to_gpr), .RAM_to_ACC(instruction_processor_1_ram_to_acc),
    .Out_to_GPR(instruction_processor_1_out_to_gpr), .Out_to_ACC(instruction_processor_1_out_to_acc),
    .Out_to_RAM(instruction_processor_1_out_to_ram), .GPR_to_RAM(instruction_processor_1_gpr_to_ram),
    .Reset(Reset), .Master_Enable(mar_tasks_1_master_enable_out),
    .GPR_to_ACC(instruction_processor_1_gpr_to_acc), .Master_Enable_Out(exec_move_1_master_enable_out));
  EXEC_ALU_Operation exec_alu_operation_1 (
    .Clock(clock_1_clock), .C1(clock_1_c1), .C3(clock_1_c3),
    .Clock_Counter(instruction_loader_1_clock_counter), .Input_A_Set(Input_A_Set),
    .GPR_Enable(exec_alu_operation_1_gpr_enable), .Use_ALU(instruction_processor_1_alu), .Reset(Reset),
    .Master_Enable(exec_move_1_master_enable_out));
  EXEC_Jump exec_jump_1 (
    .ALU_Flags(ALU_Flags), .Select(GPR_Select), .Allow_Jump(exec_jump_1_allow_jump),
    .JMP(instruction_processor_1_jmp), .Jxx(instruction_processor_1_jxx));
  Instruction_Loader instruction_loader_1 (
    .Jump_Instruction(instruction_preprocessor_1_jmp), .Save_To_RAM(instruction_preprocessor_1_out),
    .Load_IAR(instruction_preprocessor_1_ld_addr), .Load_Number(instruction_preprocessor_1_ld),
    .IER_Clock(IER_Clock), .Clock(clock_1_clock), .C1(clock_1_c1),
    .Clock_Counter(instruction_loader_1_clock_counter), .RAM_Set_A(RAM_Set), .RAM_Set_B(DEV_Set),
    .RAM_Enable(RAM_Enable), .Reset(Reset), .IAR_Set_Upper_Half(IAR_Load_U), .IAR_Set_Lower_Half(IAR_Load_L));
  Instruction_Processor instruction_processor_1 (
    .Instruction(Execute_Instruction), .ALU_Operation(ALU_Opcode), .CX(clock_1_cx), .Clear(Reset),
    .ALU(instruction_processor_1_alu), .No_Operation(instruction_processor_1_no_operation),
    .Num_to_ACC(instruction_processor_1_num_to_acc), .OUT_to_RAM(instruction_processor_1_out_to_ram),
    .GPR_to_ACC(instruction_processor_1_gpr_to_acc), .Out_to_GPR(instruction_processor_1_out_to_gpr),
    .RAM_to_GPR(instruction_processor_1_ram_to_gpr), .Num_to_GPR(instruction_processor_1_num_to_gpr),
    .JMP(instruction_processor_1_jmp), .RET(instruction_processor_1_ret),
    .CALL(instruction_processor_1_call), .OUT_to_ACC(instruction_processor_1_out_to_acc),
    .RAM_to_ACC(instruction_processor_1_ram_to_acc), .Select(GPR_Select),
    .GPR_to_RAM(instruction_processor_1_gpr_to_ram), .Jxx(instruction_processor_1_jxx));
  or or_1 (GPR_Enable, exec_move_1_gpr_enable, exec_alu_operation_1_gpr_enable);
  and and_2 (Load_From_IAR, mar_tasks_1_load_from_iar, exec_jump_1_allow_jump);

  assign GPR_Clear = Reset;
  assign IAR_Reset = Reset;
  assign IER_Reset = Reset;
  assign MAR_Reset = Reset;
endmodule

// Decoder
module Instruction_Processor (
  input  CX,
  input  [7:0] Instruction,
  input  Clear,
  output ALU,
  output Jxx,
  output [2:0] Select,
  output GPR_to_RAM,
  output GPR_to_ACC,
  output Out_to_GPR,
  output RAM_to_GPR,
  output Num_to_GPR,
  output JMP,
  output RET,
  output CALL,
  output OUT_to_ACC,
  output RAM_to_ACC,
  output OUT_to_RAM,
  output Num_to_ACC,
  output No_Operation,
  output [3:0] ALU_Operation
);

  wire and_1_out, and_2_out, and_3_out, and_4_out, and_5_out, and_6_out, and_7_out, and_8_out,
       decoder_1_out0, decoder_1_out1, decoder_1_out2, decoder_1_out3, decoder_1_out4, decoder_1_out5,
       decoder_1_out6, decoder_2_out0, decoder_2_out1, decoder_2_out2, decoder_2_out3, decoder_2_out4,
       decoder_2_out5, decoder_2_out6, decoder_2_out7, not_1_out;
  wire [3:0] register_1_q;

  D_Flip_Flop d_ff_1 (.clk(CX), .D(Instruction[7]), .Q(ALU), .reset(Clear));  // open: Qn, preset, en
  Multiplexer #(.width(4), .disabled(0), .enable("false")) multiplexer_1 (
    .in0(4'b0000), .in1(register_1_q), .out(ALU_Operation), .sel(ALU));
  Register #(.width(4)) register_1 (.D(Instruction[6:3]), .Q(register_1_q), .clk(CX), .clr(Clear));  // open: en
  D_Flip_Flop d_ff_2 (.clk(CX), .D(decoder_1_out6), .Q(Jxx), .reset(Clear));  // open: Qn, preset, en
  Decoder #(.select(4), .disabled(0)) decoder_1 (
    .out0(decoder_1_out0), .out1(decoder_1_out1), .out2(decoder_1_out2), .out3(decoder_1_out3),
    .out4(decoder_1_out4), .out5(decoder_1_out5), .out6(decoder_1_out6), .sel(Instruction[6:3]),
    .en(not_1_out));  // open: out7, out8, out9, out10, out11, out12, out13, out14, out15
  not not_1 (not_1_out, Instruction[7]);
  Register #(.width(3)) register_2 (.D(Instruction[2:0]), .Q(Select), .clk(CX), .clr(Clear));  // open: en
  Decoder #(.select(3)) decoder_2 (
    .out0(decoder_2_out0), .out1(decoder_2_out1), .out2(decoder_2_out2), .out3(decoder_2_out3),
    .out4(decoder_2_out4), .out5(decoder_2_out5), .out6(decoder_2_out6), .out7(decoder_2_out7),
    .sel(Instruction[2:0]), .en(not_1_out));
  D_Flip_Flop d_ff_3 (.clk(CX), .D(decoder_1_out5), .Q(GPR_to_RAM), .reset(Clear));  // open: Qn, preset, en
  D_Flip_Flop d_ff_4 (.clk(CX), .D(decoder_1_out4), .Q(GPR_to_ACC), .reset(Clear));  // open: Qn, preset, en
  D_Flip_Flop d_ff_5 (.clk(CX), .D(decoder_1_out3), .Q(Out_to_GPR), .reset(Clear));  // open: Qn, preset, en
  D_Flip_Flop d_ff_6 (.clk(CX), .D(decoder_1_out2), .Q(RAM_to_GPR), .reset(Clear));  // open: Qn, preset, en
  D_Flip_Flop d_ff_7 (.clk(CX), .D(decoder_1_out1), .Q(Num_to_GPR), .reset(Clear));  // open: Qn, preset, en
  and and_1 (and_1_out, decoder_2_out7, decoder_1_out0);
  D_Flip_Flop d_ff_8 (.clk(CX), .D(and_1_out), .Q(JMP), .reset(Clear));  // open: Qn, preset, en
  and and_2 (and_2_out, decoder_2_out6, decoder_1_out0);
  D_Flip_Flop d_ff_9 (.clk(CX), .D(and_2_out), .Q(RET), .reset(Clear));  // open: Qn, preset, en
  and and_3 (and_3_out, decoder_2_out5, decoder_1_out0);
  D_Flip_Flop d_ff_10 (.clk(CX), .D(and_3_out), .Q(CALL), .reset(Clear));  // open: Qn, preset, en
  and and_4 (and_4_out, decoder_2_out4, decoder_1_out0);
  D_Flip_Flop d_ff_11 (.clk(CX), .D(and_4_out), .Q(OUT_to_ACC), .reset(Clear));  // open: Qn, preset, en
  and and_5 (and_5_out, decoder_2_out3, decoder_1_out0);
  D_Flip_Flop d_ff_12 (.clk(CX), .D(and_5_out), .Q(RAM_to_ACC), .reset(Clear));  // open: Qn, preset, en
  and and_6 (and_6_out, decoder_2_out2, decoder_1_out0);
  D_Flip_Flop d_ff_13 (.clk(Clear), .D(and_6_out), .Q(OUT_to_RAM), .reset(Clear));  // open: Qn, preset, en
  and and_7 (and_7_out, decoder_2_out1, decoder_1_out0);
  D_Flip_Flop d_ff_14 (.clk(CX), .D(and_7_out), .Q(Num_to_ACC), .reset(Clear));  // open: Qn, preset, en
  and and_8 (and_8_out, decoder_2_out0, decoder_1_out0);
  D_Flip_Flop d_ff_15 (.clk(CX), .D(and_8_out), .Q(No_Operation), .reset(Clear));  // open: Qn, preset, en
endmodule

// Preloader
module Instruction_Preprocessor (
  input  [7:0] Instruction,
  output JMP,
  output OUT,
  output LD_Addr,
  output LD
);

  wire decoder_1_out0, decoder_1_out1, decoder_1_out3, decoder_1_out6, demultiplexer_1_out2,
       demultiplexer_1_out3, demultiplexer_1_out5, demultiplexer_1_out7, demultiplexer_2_out0, nand_1_out,
       nand_3_out, nand_4_out, nand_6_out, nand_7_out, nand_8_out, nand_9_out, nand_10_out, nand_11_out,
       nand_13_out, nand_14_out, nand_15_out, nand_16_out, not_1_out, not_2_out;

  nand nand_1 (nand_1_out, not_1_out, decoder_1_out6);
  Demultiplexer #(.select(3), .enable("false")) demultiplexer_1 (
    .out1(LD), .out2(demultiplexer_1_out2), .out3(demultiplexer_1_out3), .out5(demultiplexer_1_out5),
    .out7(demultiplexer_1_out7), .in(demultiplexer_2_out0), .sel(Instruction[2:0]));  // open: out0, out4, out6
  nand nand_2 (JMP, nand_1_out, nand_3_out, nand_4_out);
  nand nand_3 (nand_3_out, not_1_out, demultiplexer_1_out7);
  nand nand_4 (nand_4_out, not_1_out, decoder_1_out3);
  not not_1 (not_1_out, Instruction[3]);
  Demultiplexer #(.disabled(0), .enable("false")) demultiplexer_2 (
    .out0(demultiplexer_2_out0), .in(decoder_1_out0), .sel(Instruction[3]));  // open: out1
  nand nand_5 (OUT, nand_7_out, nand_6_out);
  nand nand_6 (nand_6_out, not_1_out, demultiplexer_1_out3);
  nand nand_7 (nand_7_out, Instruction[3], decoder_1_out3);
  nand nand_8 (nand_8_out, decoder_1_out3, Instruction[3]);
  nand nand_9 (nand_9_out, decoder_1_out1, Instruction[3]);
  Decoder #(.select(3), .disabled(0)) decoder_1 (
    .out0(decoder_1_out0), .out1(decoder_1_out1), .out3(decoder_1_out3), .out6(decoder_1_out6),
    .sel(Instruction[6:4]), .en(not_2_out));  // open: out2, out4, out5, out7
  not not_2 (not_2_out, Instruction[7]);
  nand nand_10 (nand_10_out, not_1_out, demultiplexer_1_out2);
  nand nand_11 (nand_11_out, not_1_out, demultiplexer_1_out3);
  nand nand_12 (LD_Addr, nand_9_out, nand_8_out, nand_10_out, nand_11_out, nand_14_out, nand_13_out, nand_15_out, nand_16_out);
  nand nand_13 (nand_13_out, not_1_out, demultiplexer_1_out7);
  nand nand_14 (nand_14_out, not_1_out, demultiplexer_1_out5);
  nand nand_15 (nand_15_out, not_1_out, decoder_1_out6);
  nand nand_16 (nand_16_out, not_1_out, decoder_1_out3);
endmodule

// Loader
module Instruction_Loader (
  input  Clock,
  input  C1,
  input  Jump_Instruction,
  input  Save_To_RAM,
  input  Load_IAR,
  input  Load_Number,
  input  Reset,
  output [4:0] Clock_Counter,
  output RAM_Set_A,
  output RAM_Set_B,
  output RAM_Enable,
  output IAR_Set_Upper_Half,
  output IAR_Set_Lower_Half,
  output IER_Clock
);

  wire and_1_out, and_2_out, and_3_out, and_4_out, and_5_out, and_6_out, and_7_out, and_8_out, and_9_out,
       and_10_out, and_11_out, nand_1_out, nand_2_out, nand_3_out, nand_4_out, nand_5_out, nand_6_out,
       nor_1_out, nor_2_out, not_1_out, not_2_out, not_3_out, not_4_out, not_5_out, not_6_out, not_7_out,
       not_8_out, not_9_out, not_10_out, not_11_out, not_12_out, or_1_out, or_2_out, or_3_out, or_4_out,
       or_5_out, or_6_out, or_7_out, or_8_out, or_9_out, t_ff_1_qn, t_ff_2_qn, t_ff_3_qn, t_ff_4_qn,
       t_ff_5_qn, t_ff_6_qn;
  wire [2:0] counter_1_q;

  and and_1 (and_1_out, Jump_Instruction, Load_IAR, ~Load_Number);  // AND_Gate
  and and_2 (and_2_out, ~Load_Number, Load_IAR, Save_To_RAM);  // AND_Gate
  and and_3 (and_3_out, Load_IAR, nor_1_out);
  nor nor_1 (nor_1_out, Jump_Instruction, Save_To_RAM, Load_Number);
  and and_4 (and_4_out, ~Load_IAR, Load_Number);  // AND_Gate
  nor nor_2 (nor_2_out, Load_IAR, Load_Number);
  Counter #(.width(3), .max('h7), .trigger("falling")) counter_1 (
    .Q(counter_1_q), .clk(Clock), .clr(or_1_out));  // open: load, D, count, carry
  Decoder #(.select(3), .disabled(0), .enable("false")) decoder_1 (
    .out0(Clock_Counter[0]), .out1(Clock_Counter[1]), .out2(Clock_Counter[2]), .out3(Clock_Counter[3]),
    .out4(Clock_Counter[4]), .sel(counter_1_q));  // open: out5, out6, out7
  or or_1 (or_1_out, nand_5_out, Reset);
  not not_1 (not_1_out, nand_5_out);
  not not_2 (not_2_out, not_1_out);
  or or_2 (or_2_out, and_1_out, and_2_out, and_3_out);
  and and_5 (and_5_out, Clock_Counter[3], Clock, and_2_out);
  and and_6 (and_6_out, Clock_Counter[3], C1, Clock, and_2_out);
  nand nand_1 (nand_1_out, Clock_Counter[3], and_2_out);
  and and_7 (and_7_out, Clock_Counter[2], C1, Clock, or_2_out);
  and and_8 (and_8_out, Clock_Counter[1], C1, Clock, or_2_out);
  and and_9 (and_9_out, Clock_Counter[0], C1, Clock);
  and and_10 (and_10_out, Clock_Counter[1], ~Clock);  // AND_Gate
  nand nand_2 (nand_2_out, Clock_Counter[3], Clock, and_1_out);
  or or_3 (or_3_out, and_2_out, and_3_out);
  nand nand_3 (nand_3_out, Clock_Counter[2], Clock, and_4_out);
  nand nand_4 (nand_4_out, Clock_Counter[1], Clock, nor_2_out);
  not not_3 (not_3_out, and_5_out);
  not not_4 (not_4_out, not_3_out);
  or or_4 (or_4_out, nand_5_out, ~Clock, Reset);  // OR_Gate
  or or_5 (or_5_out, nand_5_out, ~Clock, Reset);  // OR_Gate
  and and_11 (and_11_out, Clock, ~not_2_out, nand_1_out);  // AND_Gate
  not not_5 (not_5_out, and_11_out);
  or or_6 (or_6_out, nand_5_out, ~Clock, Reset);  // OR_Gate
  or or_7 (or_7_out, Clock_Counter[3], Reset);
  or or_8 (or_8_out, Clock_Counter[2], Reset);
  not not_6 (not_6_out, and_9_out);
  or or_9 (or_9_out, and_10_out, nand_5_out, Reset);
  nand nand_5 (nand_5_out, nand_2_out, nand_6_out, nand_3_out, nand_4_out);
  nand nand_6 (nand_6_out, Clock_Counter[4], Clock, or_3_out);
  not not_7 (not_7_out, not_5_out);
  not not_8 (not_8_out, not_7_out);
  not not_9 (not_9_out, not_10_out);
  not not_10 (not_10_out, not_6_out);
  not not_11 (not_11_out, not_8_out);
  not not_12 (not_12_out, not_9_out);
  T_Flip_Flop t_ff_1 (
    .clk(not_4_out), .T(t_ff_1_qn), .Q(RAM_Set_A), .Qn(t_ff_1_qn), .reset(or_4_out));  // open: preset, en
  T_Flip_Flop t_ff_2 (
    .clk(and_6_out), .T(t_ff_2_qn), .Q(RAM_Set_B), .Qn(t_ff_2_qn), .reset(or_5_out));  // open: preset, en
  T_Flip_Flop t_ff_3 (
    .clk(not_11_out), .T(t_ff_3_qn), .Q(RAM_Enable), .Qn(t_ff_3_qn), .reset(or_6_out));  // open: preset, en
  T_Flip_Flop t_ff_4 (
    .clk(and_7_out), .T(t_ff_4_qn), .Q(IAR_Set_Upper_Half), .Qn(t_ff_4_qn), .reset(or_7_out));  // open: preset, en
  T_Flip_Flop t_ff_5 (
    .clk(and_8_out), .T(t_ff_5_qn), .Q(IAR_Set_Lower_Half), .Qn(t_ff_5_qn), .reset(or_8_out));  // open: preset, en
  T_Flip_Flop t_ff_6 (
    .clk(not_12_out), .T(t_ff_6_qn), .Q(IER_Clock), .Qn(t_ff_6_qn), .reset(or_9_out));  // open: preset, en
endmodule

module Clock (
  input  Reset,
  output Master_Enable,
  output CX,
  output Clock,
  output C1,
  output C2,
  output C3
);

  wire clock_1_out, not_1_out, not_2_out, not_3_out, not_4_out, t_ff_1_q, t_ff_1_qn, t_ff_2_q, t_ff_2_qn;
  wire [3:0] counter_1_q;

  not not_1 (not_1_out, Reset);
  Clock_part clock_1 (.out(clock_1_out));
  T_Flip_Flop t_ff_1 (.clk(Clock), .T(t_ff_1_qn), .Q(t_ff_1_q), .Qn(t_ff_1_qn), .reset(Reset));  // open: preset, en
  T_Flip_Flop #(.trigger("falling")) t_ff_2 (
    .clk(Clock), .T(t_ff_2_qn), .Q(t_ff_2_q), .Qn(t_ff_2_qn), .reset(Reset));  // open: preset, en
  Counter #(.width(4), .max('hf)) counter_1 (
    .count(not_1_out), .Q(counter_1_q), .carry(CX), .clk(clock_1_out), .clr(Reset));  // open: load, D
  not not_2 (not_2_out, counter_1_q[3]);
  not not_3 (not_3_out, not_2_out);
  not not_4 (not_4_out, not_3_out);
  not not_5 (Clock, not_4_out);
  Decoder #(.select(2), .disabled(0), .enable("false")) decoder_1 (
    .out1(C1), .out2(C2), .out3(C3), .sel(counter_1_q[2:1]));  // open: out0
  and and_1 (Master_Enable, t_ff_1_q, t_ff_2_q);
endmodule

module MAR_Tasks (
  input  Master_Enable,
  input  Clock,
  input  C1,
  input  C2,
  input  C3,
  input  [4:0] Clock_Counter,
  input  No_Operation,
  input  Num_To_ACC,
  input  Out_To_RAM,
  input  RAM_to_ACC,
  input  Out_To_ACC,
  input  CALL,
  input  RET,
  input  Unconditional_Jump,
  input  Conditional_Jump,
  input  Num_To_GPR,
  input  RAM_To_GPR,
  input  Out_To_GPR,
  input  GPR_To_ACC,
  input  GPR_To_RAM,
  input  Use_ALU,
  input  Reset,
  output MAR_Set,
  output Load_to_Stack,
  output Load_From_Stack,
  output Load_From_IAR,
  output Master_Enable_Out
);

  wire and_1_out, and_2_out, and_3_out, and_4_out, nor_1_out, not_1_out, or_1_out, or_2_out, or_3_out,
       or_4_out, or_5_out, or_6_out, or_7_out;

  not not_1 (not_1_out, Clock);
  or or_1 (or_1_out, GPR_To_RAM, RAM_To_GPR, CALL, RAM_to_ACC, Out_To_RAM);
  or or_2 (or_2_out, Conditional_Jump, Unconditional_Jump, RET);
  and and_1 (and_1_out, not_1_out, C2);
  and and_2 (and_2_out, not_1_out, C1, Clock_Counter[1], or_1_out);
  and and_3 (and_3_out, not_1_out, C1, or_1_out, Clock_Counter[4]);
  and and_4 (and_4_out, not_1_out, C1, Clock_Counter[3], or_3_out);
  or or_3 (or_3_out, or_2_out, or_1_out);
  T_Flip_Flop t_ff_1 (.clk(and_1_out), .T(Master_Enable), .Q(MAR_Set), .reset(or_4_out));  // open: Qn, preset, en
  or or_4 (or_4_out, Reset, nor_1_out, C3);
  T_Flip_Flop t_ff_2 (.clk(and_2_out), .T(Master_Enable), .Q(Load_to_Stack), .reset(or_5_out));  // open: Qn, preset, en
  or or_5 (or_5_out, Reset, nor_1_out, C2);
  T_Flip_Flop t_ff_3 (
    .clk(and_3_out), .T(Master_Enable), .Q(Load_From_Stack), .reset(or_6_out));  // open: Qn, preset, en
  or or_6 (or_6_out, Reset, nor_1_out, C3);
  T_Flip_Flop t_ff_4 (.clk(and_4_out), .T(Master_Enable), .Q(Load_From_IAR), .reset(or_7_out));  // open: Qn, preset, en
  or or_7 (or_7_out, Reset, nor_1_out, C3);
  and and_5 (Master_Enable_Out, Master_Enable, ~nor_1_out);  // AND_Gate
  nor nor_1 (nor_1_out, Use_ALU, GPR_To_RAM, GPR_To_ACC, Out_To_GPR, RAM_To_GPR, Num_To_GPR, Conditional_Jump, Unconditional_Jump, RET, CALL, Out_To_ACC, RAM_to_ACC, Out_To_RAM, Num_To_ACC, No_Operation);
endmodule

// Jump
module EXEC_Jump (
  input  JMP,
  input  Jxx,
  input  [2:0] Select,
  input  [3:0] ALU_Flags,
  output Allow_Jump
);

  wire and_1_out, and_2_out, decoder_1_out0, decoder_1_out1, decoder_1_out2, decoder_1_out3, decoder_2_out0,
       decoder_2_out1, decoder_2_out2, decoder_2_out3, decoder_3_out0, decoder_3_out1, decoder_3_out2,
       decoder_3_out3, decoder_3_out4, decoder_3_out5, decoder_3_out6, decoder_3_out7, nand_1_out,
       nand_2_out, nand_3_out, nand_4_out, nand_5_out, nand_6_out, nand_7_out, nand_8_out, nand_9_out,
       nor_1_out, or_2_out;

  Decoder #(.select(2), .disabled(0), .enable("false")) decoder_1 (
    .out0(decoder_1_out0), .out1(decoder_1_out1), .out2(decoder_1_out2), .out3(decoder_1_out3),
    .sel(ALU_Flags[1:0]));
  Decoder #(.select(2), .disabled(0), .enable("false")) decoder_2 (
    .out0(decoder_2_out0), .out1(decoder_2_out1), .out2(decoder_2_out2), .out3(decoder_2_out3),
    .sel(ALU_Flags[3:2]));
  nand nand_1 (nand_1_out, decoder_2_out3, decoder_3_out7, and_2_out);
  nand nand_2 (nand_2_out, decoder_2_out0, decoder_3_out6, and_2_out);
  nand nand_3 (nand_3_out, decoder_2_out2, decoder_3_out5, and_2_out);
  nand nand_4 (nand_4_out, decoder_1_out3, decoder_3_out3, and_2_out);
  nand nand_5 (nand_5_out, decoder_2_out1, decoder_3_out4, and_2_out);
  nand nand_6 (nand_6_out, nand_1_out, nand_2_out, nand_3_out, nand_5_out, nand_4_out, nand_7_out, nand_8_out, nand_9_out);
  or or_1 (Allow_Jump, and_1_out, nor_1_out, nand_6_out);
  nand nand_7 (nand_7_out, decoder_1_out2, decoder_3_out2, and_2_out);
  nand nand_8 (nand_8_out, decoder_1_out1, decoder_3_out1, and_2_out);
  and and_1 (and_1_out, ~Jxx, JMP);  // AND_Gate
  nor nor_1 (nor_1_out, JMP, Jxx);
  and and_2 (and_2_out, ~JMP, Jxx);  // AND_Gate
  Decoder #(.select(3), .disabled(0), .enable("false")) decoder_3 (
    .out0(decoder_3_out0), .out1(decoder_3_out1), .out2(decoder_3_out2), .out3(decoder_3_out3),
    .out4(decoder_3_out4), .out5(decoder_3_out5), .out6(decoder_3_out6), .out7(decoder_3_out7), .sel(Select));
  or or_2 (or_2_out, decoder_1_out2, decoder_1_out1, decoder_1_out0);
  nand nand_9 (nand_9_out, or_2_out, decoder_3_out0, and_2_out);
endmodule

// Move
module EXEC_Move (
  input  Master_Enable,
  input  Clock,
  input  C1,
  input  C3,
  input  CX,
  input  Num_to_GPR,
  input  [4:0] Clock_Counter,
  input  Num_to_ACC,
  input  RAM_to_GPR,
  input  RAM_to_ACC,
  input  Out_to_GPR,
  input  Out_to_ACC,
  input  Out_to_RAM,
  input  GPR_to_RAM,
  input  GPR_to_ACC,
  input  Reset,
  output ACC_Set,
  output GPR_Set,
  output GPR_Enable,
  output Out_Enable,
  output Master_Enable_Out
);

  wire and_1_out, and_2_out, and_3_out, and_4_out, and_5_out, and_6_out, and_7_out, and_8_out, and_9_out,
       nor_1_out, not_1_out, not_2_out, not_3_out, not_4_out, or_1_out, or_2_out, or_3_out, or_4_out,
       or_5_out, or_6_out, or_7_out, or_8_out, or_9_out, or_10_out, or_11_out, or_12_out, or_13_out,
       or_14_out, or_15_out, or_16_out, t_ff_1_q, t_ff_2_q, t_ff_3_q, t_ff_4_q;

  or or_1 (or_1_out, and_1_out, and_2_out);
  and and_1 (and_1_out, Clock_Counter[1], or_2_out);
  and and_2 (and_2_out, Clock_Counter[3], or_3_out);
  or or_2 (or_2_out, Num_to_ACC, Num_to_GPR);
  and and_3 (and_3_out, Clock_Counter[1], or_4_out);
  and and_4 (and_4_out, Clock_Counter[3], or_5_out);
  or or_3 (or_3_out, RAM_to_ACC, RAM_to_GPR);
  or or_4 (or_4_out, GPR_to_ACC, Out_to_ACC, Out_to_GPR);
  not not_1 (not_1_out, and_4_out);
  not not_2 (not_2_out, and_5_out);
  and and_5 (and_5_out, Clock_Counter[1], or_6_out);
  or or_5 (or_5_out, GPR_to_RAM, Out_to_RAM);
  or or_6 (or_6_out, GPR_to_ACC, Out_to_ACC, Out_to_GPR);
  not not_3 (not_3_out, not_1_out);
  not not_4 (not_4_out, not_2_out);
  and and_6 (and_6_out, Clock, or_1_out, C1);
  and and_7 (and_7_out, ~Clock, C1, and_3_out);  // AND_Gate
  and and_8 (and_8_out, Clock, not_3_out);
  and and_9 (and_9_out, ~Clock, not_4_out);  // AND_Gate
  T_Flip_Flop t_ff_1 (.clk(and_6_out), .T(Master_Enable), .Q(t_ff_1_q), .reset(or_7_out));  // open: Qn, preset, en
  or or_7 (or_7_out, Reset, nor_1_out, CX);
  T_Flip_Flop t_ff_2 (.clk(and_7_out), .T(Master_Enable), .Q(t_ff_2_q), .reset(or_8_out));  // open: Qn, preset, en
  or or_8 (or_8_out, Reset, nor_1_out, C3);
  T_Flip_Flop t_ff_3 (.clk(and_8_out), .T(Master_Enable), .Q(t_ff_3_q), .reset(or_9_out));  // open: Qn, preset, en
  or or_9 (or_9_out, Reset, nor_1_out, CX);
  T_Flip_Flop t_ff_4 (.clk(and_9_out), .T(Master_Enable), .Q(t_ff_4_q), .reset(or_10_out));  // open: Qn, preset, en
  or or_10 (or_10_out, Reset, nor_1_out, C3);
  or or_11 (or_11_out, t_ff_1_q, t_ff_2_q);
  or or_12 (or_12_out, t_ff_3_q, t_ff_4_q);
  or or_13 (or_13_out, GPR_to_ACC, GPR_to_RAM);
  or or_14 (or_14_out, GPR_to_ACC, Out_to_ACC, RAM_to_ACC, Num_to_ACC);
  or or_15 (or_15_out, Out_to_RAM, Out_to_ACC, Out_to_GPR);
  or or_16 (or_16_out, Out_to_GPR, RAM_to_GPR, Num_to_GPR);
  nor nor_1 (nor_1_out, Num_to_GPR, Num_to_ACC, RAM_to_GPR, RAM_to_ACC, Out_to_GPR, Out_to_ACC, Out_to_RAM, GPR_to_RAM, GPR_to_ACC);
  and and_10 (ACC_Set, or_11_out, or_14_out);
  and and_11 (GPR_Set, or_11_out, or_16_out);
  and and_12 (GPR_Enable, or_12_out, or_13_out);
  and and_13 (Out_Enable, or_12_out, or_15_out);

  assign Master_Enable_Out = Master_Enable;
endmodule

// ALU Op
module EXEC_ALU_Operation (
  input  Master_Enable,
  input  Clock,
  input  C1,
  input  C3,
  input  Use_ALU,
  input  [4:0] Clock_Counter,
  input  Reset,
  output Input_A_Set,
  output GPR_Enable
);

  wire and_1_out, and_2_out, not_1_out, not_2_out, or_1_out;

  not not_1 (not_1_out, not_2_out);
  not not_2 (not_2_out, Use_ALU);
  and and_1 (and_1_out, ~Clock, Clock_Counter[1], C1, not_1_out);  // AND_Gate
  T_Flip_Flop t_ff_1 (.clk(and_1_out), .T(Master_Enable), .Q(Input_A_Set), .reset(or_1_out));  // open: Qn, preset, en
  and and_2 (and_2_out, ~Clock, Clock_Counter[1], not_1_out);  // AND_Gate
  T_Flip_Flop t_ff_2 (.clk(and_2_out), .T(Master_Enable), .Q(GPR_Enable), .reset(or_1_out));  // open: Qn, preset, en
  or or_1 (or_1_out, C3, Reset, ~Use_ALU);  // OR_Gate
endmodule
