// Logisim project CPU Registers.circ as structural Verilog: 3 circuits, main circuit Instruction Address Register
// IAR
module Instruction_Address_Register (
  input  Set_Lower_Half,
  input  [7:0] Address_In,
  input  Reset,
  input  Set_Upper_Half,
  output [15:0] To_MAR
);

  Register register_1 (.D(Address_In), .Q(To_MAR[7:0]), .clk(Set_Lower_Half), .clr(Reset));  // open: en
  Register register_2 (.D(Address_In), .Q(To_MAR[15:8]), .clk(Set_Upper_Half), .clr(Reset));  // open: en
endmodule

// IER
module Instruction_Execution_Register (
  input  [7:0] Instruction_Input,
  input  Reset,
  input  Clock,
  output [7:0] Instruction_Output
);

  Register register_1 (.D(Instruction_Input), .Q(Instruction_Output), .clk(Clock), .clr(Reset));  // open: en
endmodule

// MAR
module Memory_Address_Register (
  input  [15:0] From_Stack,
  input  Set_Current,
  input  Reset,
  input  Load_From_Return,
  input  Load_From_IAR,
  input  [15:0] From_IAR,
  output [15:0] To_Stack,
  output [15:0] ADDR
);

  wire [15:0] adder_1_out, multiplexer_1_out, multiplexer_2_out;

  Multiplexer #(.width(16), .enable("false")) multiplexer_1 (
    .in0(multiplexer_2_out), .in1(From_IAR), .out(multiplexer_1_out), .sel(Load_From_IAR));
  Multiplexer #(.width(16), .enable("false")) multiplexer_2 (
    .in0(adder_1_out), .in1(From_Stack), .out(multiplexer_2_out), .sel(Load_From_Return));
  Register #(.width(16)) Current (.D(multiplexer_1_out), .Q(ADDR), .clk(Set_Current), .clr(Reset));  // open: en
  Adder #(.width(16)) adder_1 (.a(ADDR), .b({16{1'b0}}), .out(adder_1_out), .cin(1'b1));  // open: cout

  assign To_Stack = ADDR;
endmodule
