// Logisim project Demo CPU Restored.circ as structural Verilog: 16 circuits, main circuit CPUCore
module CPUCore (
  input  Interrupt
);

  wire button_1_out, button_2_out, clearram_1_clockout, clearram_1_resetout, controlunit_1_acc_re,
       controlunit_1_acc_we, controlunit_1_adr_addr, controlunit_1_adr_rh, controlunit_1_adr_rl,
       controlunit_1_adr_wh, controlunit_1_adr_wl, controlunit_1_alu_en, controlunit_1_flags_from_bus,
       controlunit_1_flags_re, controlunit_1_flags_we, controlunit_1_gpr_re, controlunit_1_gpr_we,
       controlunit_1_int_disable, controlunit_1_int_enable, controlunit_1_ir_we, controlunit_1_isr_wh,
       controlunit_1_isr_wl, controlunit_1_out_re, controlunit_1_out_we, controlunit_1_pc_from_isr,
       controlunit_1_pc_ld, controlunit_1_pc_rh, controlunit_1_pc_rl, controlunit_1_pc_we,
       controlunit_1_ram_re, controlunit_1_ram_we, controlunit_1_sp_addr, controlunit_1_sp_dec,
       controlunit_1_sp_inc, dipswitch_1_sw1, dipswitch_1_sw2, interruptsystem_1_interruptout, MainClock_out,
       nor_1_out, or_1_out, or_2_out, ramgate_1_clockout, ramgate_1_loadout, ramgate_1_storeout, s_r_ff_1_q;
  wire [1:0] arithmaticlogicunit_1_flagsout, flags_1_flagsoutalu, flags_1_flagsoutcu;
  wire [2:0] controlunit_1_regselect;
  wire [3:0] controlunit_1_aluoperation;
  wire [7:0] address_1_addressout, address_1_addressout_2, arithmaticlogicunit_1_output, clearram_1_dataout,
       gpr_block_1_stack_pointer_out, gpr_block_1_to_alu, instructionreg_1_instructionout,
       programcounter_1_addressout, programcounter_1_addressout_2;
  wire [15:0] clearram_1_addrout, interruptsystem_1_isrout, multiplexer_1_out, multiplexer_2_out,
       ramgate_1_addrout;

  Button button_1 (.out(button_1_out));
  Button button_2 (.out(button_2_out));
  DipSwitch #(.number(2)) dipswitch_1 (.sw1(dipswitch_1_sw1), .sw2(dipswitch_1_sw2));
  or or_1 (or_1_out, button_1_out, dipswitch_1_sw1);
  ClearRAM clearram_1 (
    .ResetIn(or_1_out), .ResetOut(clearram_1_resetout), .DataOut(clearram_1_dataout),
    .AddrOut(clearram_1_addrout), .ClockOut(clearram_1_clockout));
  Clock MainClock (.out(MainClock_out));
  or or_2 (or_2_out, clearram_1_resetout, button_2_out, dipswitch_1_sw2);
  S_R_Flip_Flop #(.trigger("high")) s_r_ff_1 (
    .Q(s_r_ff_1_q), .reset(nor_1_out), .preset(or_2_out));  // open: S, R, clk, Qn
  nor nor_1 (nor_1_out, MainClock_out, or_2_out);
  ArithmaticLogicUnit arithmaticlogicunit_1 (
    .Output(arithmaticlogicunit_1_output), .FlagsOut(arithmaticlogicunit_1_flagsout),
    .InputA(clearram_1_dataout), .InputB(gpr_block_1_to_alu), .EN(controlunit_1_alu_en),
    .Operation(controlunit_1_aluoperation), .FlagsIn(flags_1_flagsoutalu));
  Flags flags_1 (
    .FlagsOutALU(flags_1_flagsoutalu), .FlagsOutCU(flags_1_flagsoutcu),
    .FlagsIn(arithmaticlogicunit_1_flagsout), .WE(controlunit_1_flags_we), .CLK(MainClock_out),
    .Reset(s_r_ff_1_q));
  InstructionReg instructionreg_1 (
    .InstructionOut(instructionreg_1_instructionout), .InstructionIn(clearram_1_dataout),
    .WE(controlunit_1_ir_we), .CLK(MainClock_out), .Reset(s_r_ff_1_q));
  assign clearram_1_dataout = controlunit_1_flags_re ? {{6{1'b0}}, flags_1_flagsoutcu} : 8'bz;  // Controlled_Buffer controlled_buffer_1
  InterruptSystem interruptsystem_1 (
    .InterruptOut(interruptsystem_1_interruptout), .ISROut(interruptsystem_1_isrout),
    .InterruptIn(Interrupt), .INT_ENABLE(controlunit_1_int_enable), .INT_DISABLE(controlunit_1_int_disable),
    .Clock(MainClock_out), .DataIn(clearram_1_dataout), .ISR_WL(controlunit_1_isr_wl),
    .ISR_WH(controlunit_1_isr_wh), .Clear(s_r_ff_1_q));
  Address address_1 (
    .AddressOut({address_1_addressout_2, address_1_addressout}), .Data_In(clearram_1_dataout),
    .WEL(controlunit_1_adr_wl), .WEH(controlunit_1_adr_wh), .CLK(MainClock_out), .Reset(s_r_ff_1_q));
  ControlUnit controlunit_1 (
    .RegSelect(controlunit_1_regselect), .RAM_RE(controlunit_1_ram_re), .PC_WE(controlunit_1_pc_we),
    .ADR_RL(controlunit_1_adr_rl), .ADR_RH(controlunit_1_adr_rh), .FLAGS_RE(controlunit_1_flags_re),
    .ACC_RE(controlunit_1_acc_re), .FLAGS_FROM_BUS(controlunit_1_flags_from_bus),
    .PC_FROM_ISR(controlunit_1_pc_from_isr), .GPR_RE(controlunit_1_gpr_re), .GPR_WE(controlunit_1_gpr_we),
    .SP_INC(controlunit_1_sp_inc), .SP_DEC(controlunit_1_sp_dec), .SP_ADDR(controlunit_1_sp_addr),
    .PC_RL(controlunit_1_pc_rl), .PC_RH(controlunit_1_pc_rh), .PC_LD(controlunit_1_pc_ld),
    .ADR_WL(controlunit_1_adr_wl), .ADR_WH(controlunit_1_adr_wh), .ADR_ADDR(controlunit_1_adr_addr),
    .RAM_WE(controlunit_1_ram_we), .ACC_WE(controlunit_1_acc_we), .FLAGS_WE(controlunit_1_flags_we),
    .OUT_RE(controlunit_1_out_re), .OUT_WE(controlunit_1_out_we), .ALU_EN(controlunit_1_alu_en),
    .INT_ENABLE(controlunit_1_int_enable), .INT_DISABLE(controlunit_1_int_disable),
    .ISR_WL(controlunit_1_isr_wl), .ISR_WH(controlunit_1_isr_wh), .ALUOperation(controlunit_1_aluoperation),
    .IR_WE(controlunit_1_ir_we), .Flags(flags_1_flagsoutcu), .Instruction(instructionreg_1_instructionout),
    .Interrupt(interruptsystem_1_interruptout), .Reset(s_r_ff_1_q), .CLK(MainClock_out));  // open: OUT_FROM_BUS
  assign clearram_1_dataout = controlunit_1_pc_rl ? programcounter_1_addressout_2 : 8'bz;  // Controlled_Buffer controlled_buffer_2
  ProgramCounter programcounter_1 (
    .AddressOut({programcounter_1_addressout_2, programcounter_1_addressout}), .CLK(MainClock_out),
    .FromISR(controlunit_1_pc_from_isr), .AddressIn({address_1_addressout_2, address_1_addressout}),
    .LD(controlunit_1_pc_ld), .WE(controlunit_1_pc_we), .Reset(s_r_ff_1_q), .ISROut(interruptsystem_1_isrout));
  Multiplexer #(.enable("false"), .width(16)) multiplexer_1 (
    .in0({programcounter_1_addressout_2, programcounter_1_addressout}),
    .in1({address_1_addressout_2, address_1_addressout}), .out(multiplexer_1_out),
    .sel(controlunit_1_adr_addr));
  assign clearram_1_dataout = controlunit_1_adr_rh ? address_1_addressout_2 : 8'bz;  // Controlled_Buffer controlled_buffer_3
  assign clearram_1_dataout = controlunit_1_pc_rh ? programcounter_1_addressout : 8'bz;  // Controlled_Buffer controlled_buffer_4
  Multiplexer #(.enable("false"), .width(16)) multiplexer_2 (
    .in0(multiplexer_1_out), .in1({8'h8, gpr_block_1_stack_pointer_out}), .out(multiplexer_2_out),
    .sel(controlunit_1_sp_addr));
  assign clearram_1_dataout = controlunit_1_adr_rl ? address_1_addressout : 8'bz;  // Controlled_Buffer controlled_buffer_5
  RAM #(.addrWidth(16), .databus("bidir")) Main_RAM (
    .addr(ramgate_1_addrout), .data(clearram_1_dataout));  // open: we, oe, clk
  RAMGate ramgate_1 (
    .AddrOut(ramgate_1_addrout), .LoadOut(ramgate_1_loadout), .StoreOut(ramgate_1_storeout),
    .ClockOut(ramgate_1_clockout), .AddrIn(multiplexer_2_out), .ClearAddr(clearram_1_addrout),
    .LoadIn(controlunit_1_ram_re), .StoreIn(controlunit_1_ram_we), .ClockIn(MainClock_out),
    .ClearClock(clearram_1_clockout), .ClearEnable(clearram_1_resetout));
  GPR_Block gpr_block_1 (
    .To_ALU(gpr_block_1_to_alu), .Stack_Pointer_Out(gpr_block_1_stack_pointer_out),
    .Data_Out(clearram_1_dataout), .IncSP(controlunit_1_sp_inc), .DecSP(controlunit_1_sp_dec),
    .ACC_WE(controlunit_1_acc_we), .ACC_In(clearram_1_dataout), .OUT_WE(controlunit_1_out_we),
    .OUT_In(arithmaticlogicunit_1_output), .WE(controlunit_1_gpr_we), .Data_In(clearram_1_dataout),
    .OUT_RE(controlunit_1_out_re), .RE(controlunit_1_gpr_re), .Register_Select(controlunit_1_regselect),
    .Clock(MainClock_out), .Clear(s_r_ff_1_q), .ACC_RE(controlunit_1_acc_re));

  // Notes on the sheet:
  //   Clear RAM
  //   Reset CPU
endmodule

// Control Unit
module ControlUnit (
  input  Interrupt,
  input  CLK,
  input  Reset,
  input  [1:0] Flags,
  input  [7:0] Instruction,
  output IR_WE,
  output RAM_RE,
  output PC_WE,
  output GPR_RE,
  output GPR_WE,
  output SP_INC,
  output SP_DEC,
  output SP_ADDR,
  output PC_RL,
  output PC_RH,
  output PC_LD,
  output ADR_WL,
  output ADR_WH,
  output ADR_ADDR,
  output RAM_WE,
  output ACC_WE,
  output FLAGS_WE,
  output OUT_RE,
  output OUT_WE,
  output ALU_EN,
  output INT_ENABLE,
  output INT_DISABLE,
  output ISR_WL,
  output ISR_WH,
  output ADR_RL,
  output ADR_RH,
  output FLAGS_RE,
  output ACC_RE,
  output FLAGS_FROM_BUS,
  output OUT_FROM_BUS,
  output PC_FROM_ISR,
  output [3:0] ALUOperation,
  output [2:0] RegSelect
);

  wire and_2_out, and_3_out, buffer_1_out, comparator_1_lt, comparator_2_eq, comparator_3_eq,
       comparator_4_eq, nor_1_out, not_1_out, or_1_out, or_2_out, priority_encoder_1_p5,
       priority_encoder_1_p6, priority_encoder_1_p7, stepper_1_setep2low, stepper_1_setep3low,
       stepper_1_step0high, stepper_1_step1high, stepper_1_step1low, stepper_1_step2high, stepper_1_step3high;
  wire [1:0] and_1_out, bit_extender_2_out, priority_encoder_1_p4;
  wire [2:0] bitfinder_1_index;
  wire [31:0] All_Other_Instructions_data, and_4_out, and_5_out, and_6_out, and_7_out, bit_extender_1_out,
       bit_extender_3_out, bit_extender_4_out, bit_extender_5_out, bit_extender_6_out, bit_extender_7_out,
       Conditional_Jump_data, Extra_No_Operand_Instructions_data, No_Operand_Instructions_data;
  wire [31:8] or_6_out;

  BitFinder #(.\type ("high1")) bitfinder_1 (.in(Instruction), .index(bitfinder_1_index));  // open: found
  not not_1 (not_1_out, Instruction[7]);
  or or_1 (or_1_out, or_6_out[23], Reset);
  Stepper stepper_1 (
    .Step3High(stepper_1_step3high), .Step0Low(IR_WE), .Step0High(stepper_1_step0high),
    .Step1Low(stepper_1_step1low), .Step1High(stepper_1_step1high), .Setep2Low(stepper_1_setep2low),
    .Step2High(stepper_1_step2high), .Setep3Low(stepper_1_setep3low), .Reset(or_1_out), .CLK(CLK));  // open: Setep4Low, Step4High
  buf buffer_1 (buffer_1_out, stepper_1_step0high);
  or or_2 (or_2_out, stepper_1_step1low, stepper_1_step1high);
  // Priority_Encoder #(.select(2)) priority_encoder_1: pin names not known; wires that end beside it: Interrupt, buffer_1_out, or_2_out, priority_encoder_1_p4, priority_encoder_1_p5, priority_encoder_1_p6, priority_encoder_1_p7
  assign and_1_out = priority_encoder_1_p4 & bit_extender_2_out;  // AND_Gate and_1, 2 bits wide
  assign bit_extender_1_out = {{31{not_1_out}}, not_1_out};  // Bit_Extender bit_extender_1
  or or_3 (priority_encoder_1_p5, stepper_1_setep2low, stepper_1_step2high);
  or or_4 (priority_encoder_1_p6, stepper_1_setep3low, stepper_1_step3high);
  or or_5 (priority_encoder_1_p7, buffer_1_out, or_2_out, priority_encoder_1_p5, priority_encoder_1_p6);
  assign bit_extender_2_out = {{1{priority_encoder_1_p7}}, priority_encoder_1_p7};  // Bit_Extender bit_extender_2
  ROM #(.addrWidth(6), .dataWidth(32)) No_Operand_Instructions (
    .addr({Instruction[2:0], and_1_out, CLK}), .data(No_Operand_Instructions_data));
  ROM #(.dataWidth(32)) Conditional_Jump (
    .addr({Instruction[2:0], Flags, and_1_out, CLK}), .data(Conditional_Jump_data));
  ROM #(.addrWidth(6), .dataWidth(32)) Extra_No_Operand_Instructions (
    .addr({Instruction[2:0], and_1_out, CLK}), .data(Extra_No_Operand_Instructions_data));
  ROM #(.dataWidth(32)) All_Other_Instructions (
    .addr({Instruction[7:3], and_1_out, CLK}), .data(All_Other_Instructions_data));
  assign bit_extender_3_out = {{31{priority_encoder_1_p7}}, priority_encoder_1_p7};  // Bit_Extender bit_extender_3
  assign bit_extender_4_out = {{31{comparator_1_lt}}, comparator_1_lt};  // Bit_Extender bit_extender_4
  Comparator #(.mode("unsigned"), .width(3)) comparator_1 (
    .a(bitfinder_1_index), .b(3'b011), .lt(comparator_1_lt));  // open: gt, eq
  assign bit_extender_5_out = {{31{comparator_2_eq}}, comparator_2_eq};  // Bit_Extender bit_extender_5
  Comparator #(.mode("unsigned"), .width(4)) comparator_2 (
    .a(Instruction[6:3]), .b(4'b0110), .eq(comparator_2_eq));  // open: gt, lt
  Comparator #(.mode("unsigned"), .width(4)) comparator_3 (
    .a(Instruction[6:3]), .b(4'b1101), .eq(comparator_3_eq));  // open: gt, lt
  and and_2 (and_2_out, comparator_3_eq, not_1_out);
  Comparator #(.mode("unsigned")) comparator_4 (.a(Instruction), .b(8'h70), .eq(comparator_4_eq));  // open: gt, lt
  and and_3 (and_3_out, comparator_4_eq, not_1_out);
  assign bit_extender_6_out = {{31{nor_1_out}}, nor_1_out};  // Bit_Extender bit_extender_6
  nor nor_1 (nor_1_out, and_3_out, comparator_2_eq, comparator_1_lt, and_2_out);
  assign bit_extender_7_out = {{31{and_2_out}}, and_2_out};  // Bit_Extender bit_extender_7
  assign and_4_out = bit_extender_3_out & No_Operand_Instructions_data & bit_extender_4_out & bit_extender_1_out;  // AND_Gate and_4, 32 bits wide
  assign and_5_out = bit_extender_3_out & Conditional_Jump_data & bit_extender_5_out & bit_extender_1_out;  // AND_Gate and_5, 32 bits wide
  assign and_6_out = bit_extender_3_out & Extra_No_Operand_Instructions_data & bit_extender_7_out & bit_extender_1_out;  // AND_Gate and_6, 32 bits wide
  assign and_7_out = bit_extender_3_out & All_Other_Instructions_data & bit_extender_6_out;  // AND_Gate and_7, 32 bits wide
  assign {or_6_out[31:28], ISR_WH, ISR_WL, INT_DISABLE, INT_ENABLE, or_6_out[23:20], ALU_EN, OUT_WE, OUT_RE, or_6_out[16], FLAGS_WE, ACC_WE, RAM_WE, or_6_out[12], ADR_ADDR, ADR_WH, ADR_WL, or_6_out[8], PC_LD, PC_RH, PC_RL, SP_ADDR, SP_DEC, SP_INC, GPR_WE, GPR_RE} = and_4_out | and_5_out | and_6_out | and_7_out;  // OR_Gate or_6, 32 bits wide
  or or_7 (RAM_RE, IR_WE, or_6_out[12]);
  or or_8 (PC_WE, IR_WE, or_6_out[8]);

  assign ACC_RE = 1'b0;
  assign ADR_RH = 1'b0;
  assign ADR_RL = 1'b0;
  assign ALUOperation = Instruction[6:3];
  assign FLAGS_FROM_BUS = 1'b0;
  assign FLAGS_RE = 1'b0;
  assign OUT_FROM_BUS = 1'b0;
  assign PC_FROM_ISR = 1'b0;
  assign RegSelect = Instruction[2:0];

  // Notes on the sheet:
  //   contents of No_Operand_Instructions (hex, n*v repeats v):
  //   0 0 800000 6*0 5100 800000 6*0 1300 1500 0 22800 0 800000 0 0 1300 1500 5800 800000 4*0 24000 800000
  //   6*0 1308 1500 0 2030 8 2050 180 0 1214 1410 184 800000 4*0 1300 1500 180 800000
  //   contents of Conditional_Jump (hex, n*v repeats v):
  //   0 1300 1500 180 800000 4*0 100 100 0 800000 4*0 1300 1500 180 800000 4*0 100 100 0 800000 4*0 100
  //   100 0 800000 4*0 1300 1500 180 800000 4*0 100 100 0 800000 4*0 1300 1500 180 800000 4*0 100 100 0
  //   800000 4*0 100 100 0 800000 4*0 1300 1500 180 800000 4*0 1300 1500 180 800000 4*0 1300 1500 180
  //   800000 4*0 1300 1500 180 800000 4*0 100 100 0 800000 4*0 100 100 0 800000 4*0 1300 1500 180 800000
  //   4*0 100 100 0 800000 4*0 100 100 0 800000 4*0 100 100 0 800000 4*0 100 100 0 800000 4*0 1300 1500
  //   180 800000 4*0 1300 1500 180 800000 4*0 100 100 0 800000
  //   contents of Extra_No_Operand_Instructions (hex, n*v repeats v):
  //   0 1300 800000 7*0 1500 0 800000 4*0 20200 800000 7*0 401 0 800000 20*0 1300 1500 0 800000 4*0 5800
  //   800000
  //   contents of All_Other_Instructions (hex, n*v repeats v):
  //   9*0 1102 800000 6*0 1300 1500 1802 800000 4*0 20002 800000 6*0 4001 800000 6*0 1300 1500 0 2801 0
  //   800000 10*0 1802 800000 7*0 2801 0 800000 4*0 8 2011 0 800000 4*0 1016 800000 6*0 201 800000 7*0 401
  //   0 800000 28*0 c8001 800000 6*0 c8001 800000 6*0 c8001 800000 6*0 c8001 800000 6*0 c8001 800000 6*0
  //   c8001 800000 6*0 88001 800000 6*0 c8001 800000 6*0 c8001 800000 6*0 c8001 800000 6*0 c8001 800000
  //   6*0 c8001 800000 6*0 c8001 800000 6*0 c8001 800000 6*0 c8001 800000 6*0 88001 800000
endmodule

// Arithmatic Logic Unit
module ArithmaticLogicUnit (
  input  [7:0] InputA,
  input  [7:0] InputB,
  input  [1:0] FlagsIn,
  input  EN,
  input  [3:0] Operation,
  output [7:0] Output,
  output [1:0] FlagsOut
);

  wire advancedadder_1_cout;
  wire [2:0] bit_extender_1_out;
  wire [7:0] advancedadder_1_sum, and_1_out, nand_1_out, nor_1_out, not_1_out, or_1_out, shifter_1_out,
       shifter_2_out, xor_1_out;

  AdvancedAdder advancedadder_1 (
    .Sum(advancedadder_1_sum), .Cout(advancedadder_1_cout), .Cin(FlagsIn[1]), .Enable(EN),
    .Operation(Operation), .A(InputA), .B(InputB));
  assign and_1_out = InputA & InputB;  // AND_Gate and_1, 8 bits wide
  assign nand_1_out = ~(InputA & InputB);  // NAND_Gate nand_1, 8 bits wide
  assign or_1_out = InputA | InputB;  // OR_Gate or_1, 8 bits wide
  assign nor_1_out = ~(InputA | InputB);  // NOR_Gate nor_1, 8 bits wide
  assign not_1_out = ~InputA;  // NOT_Gate not_1, 8 bits wide
  assign xor_1_out = InputA ^ InputB;  // XOR_Gate xor_1, 8 bits wide
  Bit_Extender #(.out_width(3)) bit_extender_1 (.in(InputB), .out(bit_extender_1_out));
  Shifter #(.shift("lr")) shifter_1 (.in(InputA), .\dist (bit_extender_1_out), .out(shifter_1_out));
  Shifter shifter_2 (.in(InputA), .\dist (bit_extender_1_out), .out(shifter_2_out));
  Multiplexer #(.select(4), .width(8)) multiplexer_1 (
    .in0(advancedadder_1_sum), .in1(advancedadder_1_sum), .in2(advancedadder_1_sum),
    .in3(advancedadder_1_sum), .in4(advancedadder_1_sum), .in5(advancedadder_1_sum), .in6(InputA),
    .in7(and_1_out), .in8(nand_1_out), .in9(or_1_out), .in10(nor_1_out), .in11(not_1_out), .in12(xor_1_out),
    .in13(shifter_1_out), .in14(shifter_2_out), .in15(advancedadder_1_sum), .out(Output), .sel(Operation),
    .en(EN));
  Multiplexer #(.select(4)) multiplexer_2 (
    .in0(advancedadder_1_cout), .in1(advancedadder_1_cout), .in2(advancedadder_1_cout), .in3(1'b0),
    .in4(advancedadder_1_cout), .in5(advancedadder_1_cout), .in6(1'b0), .in7(1'b0), .in8(1'b0), .in9(1'b0),
    .in10(1'b0), .in11(1'b0), .in12(1'b0), .in13(1'b0), .in14(1'b0), .in15(advancedadder_1_cout),
    .out(FlagsOut[1]), .sel(Operation), .en(EN));
  Comparator #(.mode("unsigned")) comparator_1 (.a(Output), .b({8{1'b0}}), .eq(FlagsOut[0]));  // open: gt, lt
endmodule

module AdvancedAdder (
  input  Cin,
  input  Enable,
  input  [3:0] Operation,
  input  [7:0] A,
  input  [7:0] B,
  output [7:0] Sum,
  output Cout
);

  wire adder_1_cout, and_1_out, demultiplexer_1_out0, demultiplexer_1_out2, demultiplexer_1_out3,
       demultiplexer_1_out4, demultiplexer_1_out5, demultiplexer_1_out15, or_1_out, or_2_out, or_3_out,
       or_4_out, xor_1_out, xor_2_out;
  wire [7:0] multiplexer_1_out, multiplexer_2_out, multiplexer_3_out, multiplexer_4_out, not_1_out;

  Demultiplexer #(.enable("false"), .select(4)) demultiplexer_1 (
    .out0(demultiplexer_1_out0), .out2(demultiplexer_1_out2), .out3(demultiplexer_1_out3),
    .out4(demultiplexer_1_out4), .out5(demultiplexer_1_out5), .out15(demultiplexer_1_out15), .in(Enable),
    .sel(Operation));  // open: out1, out6, out7, out8, out9, out10, out11, out12, out13, out14
  Multiplexer #(.enable("false"), .width(8)) multiplexer_1 (
    .in0(B), .in1(A), .out(multiplexer_1_out), .sel(demultiplexer_1_out3));
  Multiplexer #(.enable("false"), .width(8)) multiplexer_2 (
    .in0(multiplexer_1_out), .in1(8'h1), .out(multiplexer_2_out), .sel(or_1_out));
  or or_1 (or_1_out, demultiplexer_1_out4, demultiplexer_1_out5);
  Multiplexer #(.enable("false"), .width(8)) multiplexer_3 (
    .in0(A), .in1({8{1'b0}}), .out(multiplexer_3_out), .sel(demultiplexer_1_out3));
  Multiplexer #(.enable("false"), .width(8)) multiplexer_4 (
    .in0(multiplexer_2_out), .in1(not_1_out), .out(multiplexer_4_out), .sel(or_2_out));
  assign not_1_out = ~multiplexer_2_out;  // NOT_Gate not_1, 8 bits wide
  or or_2 (or_2_out, demultiplexer_1_out2, demultiplexer_1_out3, demultiplexer_1_out5, demultiplexer_1_out15);
  or or_3 (or_3_out, demultiplexer_1_out3, xor_2_out);
  Adder adder_1 (.a(multiplexer_3_out), .b(multiplexer_4_out), .out(Sum), .cin(or_3_out), .cout(adder_1_cout));
  xor xor_1 (xor_1_out, adder_1_cout, or_2_out);
  xor xor_2 (xor_2_out, or_4_out, and_1_out);
  and and_1 (and_1_out, demultiplexer_1_out0, Cin);
  and and_2 (Cout, ~demultiplexer_1_out3, xor_1_out);  // AND_Gate
  or or_4 (or_4_out, demultiplexer_1_out15, demultiplexer_1_out2);
endmodule

module Address (
  input  [7:0] Data_In,
  input  WEL,
  input  WEH,
  input  CLK,
  input  Reset,
  output [15:0] AddressOut
);

  Register #(.trigger("falling")) TempLow (.D(Data_In), .en(WEL), .clk(CLK), .Q(AddressOut[7:0]), .clr(Reset));
  Register TempHigh (.D(Data_In), .en(WEH), .clk(CLK), .Q(AddressOut[15:8]), .clr(Reset));
endmodule

module Accumulator (
  input  [7:0] DataIn,
  input  WE,
  input  CLK,
  input  Reset,
  output [7:0] BusOut,
  output [7:0] DataOut
);

  Register #(.trigger("falling")) Accumulator (.D(DataIn), .en(WE), .clk(CLK), .Q(BusOut), .clr(Reset));

  assign DataOut = BusOut;
endmodule

module Output (
  input  FromBus,
  input  [7:0] BusIn,
  input  [7:0] DataIn,
  input  WE,
  input  CLK,
  input  Reset,
  input  RE,
  output [7:0] DataOut
);

  wire not_1_out;
  wire [7:0] multiplexer_1_out, Output_q;

  not not_1 (not_1_out, FromBus);
  Register #(.trigger("falling")) Output (.D(multiplexer_1_out), .en(WE), .clk(CLK), .Q(Output_q), .clr(Reset));
  Multiplexer #(.enable("false"), .width(8)) multiplexer_1 (
    .in0(BusIn), .in1(DataIn), .out(multiplexer_1_out), .sel(not_1_out));
  assign DataOut = RE ? Output_q : 8'bz;  // Controlled_Buffer controlled_buffer_1
endmodule

module Flags (
  input  [1:0] FlagsIn,
  input  WE,
  input  CLK,
  input  Reset,
  output [1:0] FlagsOutALU,
  output [1:0] FlagsOutCU
);

  Register #(.trigger("falling"), .width(2)) Flags (.D(FlagsIn), .en(WE), .clk(CLK), .Q(FlagsOutALU), .clr(Reset));

  assign FlagsOutCU = FlagsOutALU;
endmodule

// PC
module ProgramCounter (
  input  [15:0] ISROut,
  input  FromISR,
  input  [15:0] AddressIn,
  input  LD,
  input  WE,
  input  Reset,
  input  CLK,
  output [15:0] AddressOut
);

  wire dualedgegenerator_1_triggerout, not_1_out;
  wire [15:0] adder_1_out, multiplexer_1_out, multiplexer_2_out;

  not not_1 (not_1_out, FromISR);
  Adder #(.width(16)) adder_1 (.a(AddressOut), .b({16{1'b0}}), .out(adder_1_out), .cin(1'b1));  // open: cout
  Multiplexer #(.enable("false"), .width(16)) multiplexer_1 (
    .in0(adder_1_out), .in1(AddressIn), .out(multiplexer_1_out), .sel(LD));
  DualEdgeGenerator dualedgegenerator_1 (.CLKin(CLK), .TriggerOut(dualedgegenerator_1_triggerout));
  Multiplexer #(.enable("false"), .width(16)) multiplexer_2 (
    .in0(ISROut), .in1(multiplexer_1_out), .out(multiplexer_2_out), .sel(not_1_out));
  Register #(.width(16)) ProgramCounter (
    .D(multiplexer_2_out), .en(WE), .clk(dualedgegenerator_1_triggerout), .Q(AddressOut), .clr(Reset));
endmodule

// Instruction
module InstructionReg (
  input  [7:0] InstructionIn,
  input  WE,
  input  CLK,
  input  Reset,
  output [7:0] InstructionOut
);

  Register Instruction (.D(InstructionIn), .en(WE), .clk(CLK), .Q(InstructionOut), .clr(Reset));
endmodule

module Stepper (
  input  Reset,
  input  CLK,
  output Step0Low,
  output Step0High,
  output Step1Low,
  output Step1High,
  output Setep2Low,
  output Step2High,
  output Setep3Low,
  output Step3High,
  output Setep4Low,
  output Step4High
);

  wire not_1_out, or_1_out, or_2_out, or_3_out, or_4_out, or_5_out, or_6_out, or_7_out, or_8_out, or_9_out,
       s_r_ff_1_q, s_r_ff_2_q, s_r_ff_3_q, s_r_ff_4_q, s_r_ff_5_q, s_r_ff_6_q, s_r_ff_7_q, s_r_ff_8_q,
       s_r_ff_9_q, s_r_ff_10_q;

  S_R_Flip_Flop #(.trigger("falling")) s_r_ff_1 (
    .S(s_r_ff_8_q), .R(1'b0), .clk(CLK), .Q(s_r_ff_1_q), .reset(s_r_ff_2_q), .preset(Reset));  // open: Qn
  not not_1 (not_1_out, Reset);
  and and_1 (Step0Low, s_r_ff_1_q, not_1_out, ~s_r_ff_2_q);  // AND_Gate
  S_R_Flip_Flop s_r_ff_2 (.S(s_r_ff_1_q), .R(1'b0), .clk(CLK), .Q(s_r_ff_2_q), .reset(or_1_out));  // open: Qn, preset
  or or_1 (or_1_out, Reset, s_r_ff_3_q);
  S_R_Flip_Flop #(.trigger("falling")) s_r_ff_3 (
    .S(s_r_ff_2_q), .R(1'b0), .clk(CLK), .Q(s_r_ff_3_q), .reset(or_2_out));  // open: Qn, preset
  or or_2 (or_2_out, Reset, s_r_ff_4_q);
  and and_2 (Step0High, s_r_ff_2_q, not_1_out, ~s_r_ff_3_q);  // AND_Gate
  S_R_Flip_Flop s_r_ff_4 (.S(s_r_ff_3_q), .R(1'b0), .clk(CLK), .Q(s_r_ff_4_q), .reset(or_3_out));  // open: Qn, preset
  or or_3 (or_3_out, Reset, s_r_ff_5_q);
  and and_3 (Step1Low, s_r_ff_3_q, not_1_out, ~s_r_ff_4_q);  // AND_Gate
  S_R_Flip_Flop #(.trigger("falling")) s_r_ff_5 (
    .S(s_r_ff_4_q), .R(1'b0), .clk(CLK), .Q(s_r_ff_5_q), .reset(or_4_out));  // open: Qn, preset
  or or_4 (or_4_out, Reset, s_r_ff_6_q);
  and and_4 (Step1High, s_r_ff_4_q, not_1_out, ~s_r_ff_5_q);  // AND_Gate
  S_R_Flip_Flop s_r_ff_6 (.S(s_r_ff_5_q), .R(1'b0), .clk(CLK), .Q(s_r_ff_6_q), .reset(or_5_out));  // open: Qn, preset
  or or_5 (or_5_out, Reset, s_r_ff_7_q);
  and and_5 (Setep2Low, s_r_ff_5_q, not_1_out, ~s_r_ff_6_q);  // AND_Gate
  S_R_Flip_Flop #(.trigger("falling")) s_r_ff_7 (
    .S(s_r_ff_6_q), .R(1'b0), .clk(CLK), .Q(s_r_ff_7_q), .reset(or_6_out));  // open: Qn, preset
  and and_6 (Step2High, s_r_ff_6_q, not_1_out, ~s_r_ff_7_q);  // AND_Gate
  S_R_Flip_Flop s_r_ff_8 (.S(s_r_ff_7_q), .R(1'b0), .clk(CLK), .Q(s_r_ff_8_q), .reset(or_7_out));  // open: Qn, preset
  or or_6 (or_6_out, Reset, s_r_ff_8_q);
  and and_7 (Setep3Low, s_r_ff_7_q, not_1_out, ~s_r_ff_8_q);  // AND_Gate
  or or_7 (or_7_out, Reset, s_r_ff_1_q);
  and and_8 (Step3High, s_r_ff_8_q, not_1_out, ~s_r_ff_1_q);  // AND_Gate
  S_R_Flip_Flop #(.trigger("falling")) s_r_ff_9 (
    .S(s_r_ff_8_q), .R(1'b0), .clk(CLK), .Q(s_r_ff_9_q), .reset(or_8_out));  // open: Qn, preset
  or or_8 (or_8_out, Reset, s_r_ff_10_q);
  and and_9 (Setep4Low, s_r_ff_9_q, not_1_out, ~s_r_ff_10_q);  // AND_Gate
  S_R_Flip_Flop s_r_ff_10 (.S(s_r_ff_9_q), .R(1'b0), .clk(CLK), .Q(s_r_ff_10_q), .reset(or_9_out));  // open: Qn, preset
  or or_9 (or_9_out, Reset, s_r_ff_1_q);
  and and_10 (Step4High, s_r_ff_10_q, not_1_out, ~s_r_ff_1_q);  // AND_Gate
endmodule

module RAMGate (
  input  ClearEnable,
  input  [15:0] AddrIn,
  input  [15:0] ClearAddr,
  input  LoadIn,
  input  StoreIn,
  input  ClockIn,
  input  ClearClock,
  output [15:0] AddrOut,
  output LoadOut,
  output StoreOut,
  output ClockOut
);

  Multiplexer #(.enable("false"), .width(16)) multiplexer_1 (
    .in0(AddrIn), .in1(ClearAddr), .out(AddrOut), .sel(ClearEnable));
  and and_1 (LoadOut, ~ClearEnable, LoadIn);  // AND_Gate
  Multiplexer #(.enable("false")) multiplexer_2 (.in0(StoreIn), .in1(ClearEnable), .out(StoreOut), .sel(ClearEnable));
  Multiplexer #(.enable("false")) multiplexer_3 (.in0(ClockIn), .in1(ClearClock), .out(ClockOut), .sel(ClearEnable));
endmodule

module ClearRAM (
  input  ResetIn,
  output ResetOut,
  output [7:0] DataOut,
  output [15:0] AddrOut,
  output ClockOut
);

  wire counter_1_carry;
  wire [16:16] counter_1_q;

  Counter #(.max('h1ffff), .width(17)) counter_1 (
    .clr(counter_1_q[16]), .count(ResetOut), .clk(ClockOut), .carry(counter_1_carry),
    .Q({counter_1_q[16], AddrOut}));  // open: load, up, D
  Clock clock_1 (.out(ClockOut));
  S_R_Flip_Flop #(.trigger("high")) s_r_ff_1 (
    .clk(counter_1_carry), .Q(ResetOut), .reset(counter_1_q[16]), .preset(ResetIn));  // open: S, R, Qn
  assign DataOut = ResetOut ? {8{1'b0}} : 8'bz;  // Controlled_Buffer controlled_buffer_1
endmodule

module GPR_Block (
  input  [7:0] Data_In,
  input  WE,
  input  [2:0] Register_Select,
  input  ACC_WE,
  input  [7:0] ACC_In,
  input  OUT_WE,
  input  [7:0] OUT_In,
  input  IncSP,
  input  DecSP,
  input  Clock,
  input  Clear,
  input  ACC_RE,
  input  OUT_RE,
  input  RE,
  output [7:0] Data_Out,
  output [7:0] To_ALU,
  output [7:0] Stack_Pointer_Out
);

  wire demultiplexer_1_out0, demultiplexer_1_out1, demultiplexer_1_out2, demultiplexer_1_out3,
       demultiplexer_1_out4, demultiplexer_1_out5, demultiplexer_1_out6, demultiplexer_1_out7, or_1_out,
       or_2_out, or_3_out, or_4_out, or_5_out, or_6_out;
  wire [7:0] adder_1_out, multiplexer_1_out, multiplexer_2_out, multiplexer_3_out, multiplexer_4_out,
       multiplexer_5_out, multiplexer_6_out, r0_q, r1_q, r2_q, r3_q, r4_q, r6_q, subtractor_1_out;

  Adder adder_1 (.a(Stack_Pointer_Out), .b({8{1'b0}}), .out(adder_1_out), .cin(IncSP));  // open: cout
  Subtractor subtractor_1 (.a(Stack_Pointer_Out), .b({8{1'b0}}), .out(subtractor_1_out), .bin(DecSP));  // open: bout
  or or_1 (or_1_out, IncSP, DecSP);
  Multiplexer #(.enable("false"), .width(8)) multiplexer_1 (
    .in0(Data_In), .in1(multiplexer_2_out), .out(multiplexer_1_out), .sel(or_1_out));
  Multiplexer #(.enable("false"), .width(8)) multiplexer_2 (
    .in0(adder_1_out), .in1(subtractor_1_out), .out(multiplexer_2_out), .sel(DecSP));
  Demultiplexer #(.enable("false"), .select(3)) demultiplexer_1 (
    .out0(demultiplexer_1_out0), .out1(demultiplexer_1_out1), .out2(demultiplexer_1_out2),
    .out3(demultiplexer_1_out3), .out4(demultiplexer_1_out4), .out5(demultiplexer_1_out5),
    .out6(demultiplexer_1_out6), .out7(demultiplexer_1_out7), .in(WE), .sel(Register_Select));
  Multiplexer #(.enable("false"), .width(8)) multiplexer_3 (
    .in0(Data_In), .in1(ACC_In), .out(multiplexer_3_out), .sel(ACC_WE));
  Multiplexer #(.enable("false"), .width(8)) multiplexer_4 (
    .in0(Data_In), .in1(OUT_In), .out(multiplexer_4_out), .sel(OUT_WE));
  or or_2 (or_2_out, demultiplexer_1_out5, ACC_WE);
  or or_3 (or_3_out, demultiplexer_1_out6, OUT_WE);
  or or_4 (or_4_out, or_1_out, demultiplexer_1_out7);
  Register #(.trigger("falling")) r0 (.D(Data_In), .en(demultiplexer_1_out0), .clk(Clock), .Q(r0_q), .clr(Clear));
  Register #(.trigger("falling")) r1 (.D(Data_In), .en(demultiplexer_1_out1), .clk(Clock), .Q(r1_q), .clr(Clear));
  Register #(.trigger("falling")) r2 (.D(Data_In), .en(demultiplexer_1_out2), .clk(Clock), .Q(r2_q), .clr(Clear));
  Register #(.trigger("falling")) r3 (.D(Data_In), .en(demultiplexer_1_out3), .clk(Clock), .Q(r3_q), .clr(Clear));
  Register #(.trigger("falling")) r4 (.D(Data_In), .en(demultiplexer_1_out4), .clk(Clock), .Q(r4_q), .clr(Clear));
  Register #(.trigger("falling")) r5 (.D(multiplexer_3_out), .en(or_2_out), .clk(Clock), .Q(To_ALU), .clr(Clear));
  Register #(.trigger("falling")) r6 (.D(multiplexer_4_out), .en(or_3_out), .clk(Clock), .Q(r6_q), .clr(Clear));
  Register #(.trigger("falling")) r7 (
    .D(multiplexer_1_out), .en(or_4_out), .clk(Clock), .Q(Stack_Pointer_Out), .clr(Clear));
  Multiplexer #(.disabled("Z"), .enable("false"), .select(3), .width(8)) multiplexer_5 (
    .in0(r0_q), .in1(r1_q), .in2(r2_q), .in3(r3_q), .in4(r4_q), .in5(To_ALU), .in6(r6_q),
    .in7(Stack_Pointer_Out), .out(multiplexer_5_out), .sel(Register_Select));
  Multiplexer #(.disabled("Z"), .enable("false"), .width(8)) multiplexer_6 (
    .in0(To_ALU), .in1(r6_q), .out(multiplexer_6_out), .sel(OUT_RE));
  Multiplexer #(.disabled("Z"), .width(8)) multiplexer_7 (
    .in0(multiplexer_5_out), .in1(multiplexer_6_out), .out(Data_Out), .sel(or_6_out), .en(or_5_out));
  or or_5 (or_5_out, or_6_out, RE);
  or or_6 (or_6_out, ACC_RE, OUT_RE);

  // Other names for the same wires on the sheet: dIn[7:0] = Data_In; sp[7:0] = Stack_Pointer_Out
endmodule

module DualEdgeGenerator (
  input  CLKin,
  output TriggerOut
);

  wire buffer_1_out, buffer_2_out, buffer_3_out, buffer_4_out, buffer_5_out, buffer_6_out, buffer_7_out,
       buffer_8_out, buffer_9_out, buffer_10_out, buffer_11_out, buffer_12_out, xor_1_out, xor_2_out,
       xor_3_out, xor_4_out;

  xor xor_1 (xor_1_out, 1'b1, CLKin);
  xor xor_2 (xor_2_out, CLKin, 1'b0);
  buf buffer_1 (buffer_1_out, xor_1_out);
  buf buffer_2 (buffer_2_out, buffer_1_out);
  buf buffer_3 (buffer_3_out, xor_2_out);
  buf buffer_4 (buffer_4_out, buffer_3_out);
  buf buffer_5 (buffer_5_out, buffer_2_out);
  buf buffer_6 (buffer_6_out, buffer_5_out);
  buf buffer_7 (buffer_7_out, buffer_6_out);
  buf buffer_8 (buffer_8_out, buffer_7_out);
  buf buffer_9 (buffer_9_out, buffer_4_out);
  buf buffer_10 (buffer_10_out, buffer_9_out);
  buf buffer_11 (buffer_11_out, buffer_10_out);
  buf buffer_12 (buffer_12_out, buffer_11_out);
  xor xor_3 (xor_3_out, xor_1_out, buffer_8_out);
  or or_1 (TriggerOut, xor_3_out, xor_4_out);
  xor xor_4 (xor_4_out, buffer_12_out, xor_2_out);
endmodule

// Interrupt System
module InterruptSystem (
  input  InterruptIn,
  input  INT_ENABLE,
  input  INT_DISABLE,
  input  Clock,
  input  [7:0] DataIn,
  input  ISR_WL,
  input  ISR_WH,
  input  Clear,
  output InterruptOut,
  output [15:0] ISROut
);

  wire InterruptsEnabled_q;

  S_R_Flip_Flop #(.trigger("falling")) InterruptsEnabled (
    .S(INT_ENABLE), .R(INT_DISABLE), .clk(Clock), .Q(InterruptsEnabled_q));  // open: reset, Qn, preset
  Register #(.trigger("falling")) ISRLow (.D(DataIn), .en(ISR_WL), .clk(Clock), .Q(ISROut[7:0]), .clr(Clear));
  Register ISRHigh (.D(DataIn), .en(ISR_WH), .clk(Clock), .Q(ISROut[15:8]), .clr(Clear));
  and and_1 (InterruptOut, InterruptIn, InterruptsEnabled_q);
endmodule
