// Logisim project Demo CPU.circ as structural Verilog: 11 circuits, main circuit Processor
// DemoCPU
module Processor (
  input  CLK,
  input  CLR,
  input  INT,
  input  [7:0] Data_In,
  output [7:0] Data_Out,
  output RAM_WE,
  output RAM_RE,
  output [15:0] Address_Out
);

  wire control_unit_1_adr_load, control_unit_1_adr_rh, control_unit_1_adr_rl, control_unit_1_adr_wh,
       control_unit_1_adr_wl, control_unit_1_alu_en, control_unit_1_flags_load, control_unit_1_flags_re,
       control_unit_1_flags_we, control_unit_1_gpr_acc_we, control_unit_1_gpr_out_re,
       control_unit_1_gpr_out_we, control_unit_1_gpr_re, control_unit_1_gpr_sp_dec,
       control_unit_1_gpr_sp_inc, control_unit_1_gpr_we, control_unit_1_int_disable,
       control_unit_1_int_enable, control_unit_1_ir_we, control_unit_1_iss_wh, control_unit_1_iss_wl,
       control_unit_1_pc_load, control_unit_1_pc_load_iss, control_unit_1_pc_load_tmp, control_unit_1_pc_rh,
       control_unit_1_pc_rl, control_unit_1_pc_wh, control_unit_1_pc_wl, control_unit_1_tmp_dec,
       control_unit_1_tmp_from_adr, control_unit_1_tmp_inc, control_unit_1_tmp_load, control_unit_1_tmp_wh,
       control_unit_1_tmp_wl, interrupt_service_system_1_interrupt_out, nor_1_out, s_r_ff_1_q;
  wire [1:0] arithmetic_logic_unit_1_flags_out, control_unit_1_addr_sel, flags_register_1_alu_in;
  wire [2:0] control_unit_1_gpr_sel;
  wire [3:0] control_unit_1_alu_op;
  wire [7:0] arithmetic_logic_unit_1_out, instruction_register_1_instruction_out, program_counter_1_data_out,
       register_file_1_alu_in;
  wire [15:0] address_register_1_address_out, interrupt_service_system_1_address_out,
       program_counter_1_address_out, register_file_1_stack_pointer_out, temporary_register_1_address_out;

  S_R_Flip_Flop s_r_ff_1 (.Q(s_r_ff_1_q), .reset(nor_1_out), .preset(CLR));  // open: S, R, clk, Qn
  nor nor_1 (nor_1_out, CLK, CLR);
  Control_Unit control_unit_1 (
    .GPR_SEL(control_unit_1_gpr_sel), .ALU_OP(control_unit_1_alu_op), .ISS_WL(control_unit_1_iss_wl),
    .ISS_WH(control_unit_1_iss_wh), .INT_ENABLE(control_unit_1_int_enable),
    .INT_DISABLE(control_unit_1_int_disable), .TMP_WL(control_unit_1_tmp_wl), .TMP_WH(control_unit_1_tmp_wh),
    .TMP_LOAD(control_unit_1_tmp_load), .TMP_FROM_ADR(control_unit_1_tmp_from_adr),
    .TMP_INC(control_unit_1_tmp_inc), .TMP_DEC(control_unit_1_tmp_dec), .PC_WL(control_unit_1_pc_wl),
    .PC_WH(control_unit_1_pc_wh), .PC_RL(control_unit_1_pc_rl), .PC_RH(control_unit_1_pc_rh),
    .PC_LOAD(control_unit_1_pc_load), .PC_LOAD_ISS(control_unit_1_pc_load_iss),
    .PC_LOAD_TMP(control_unit_1_pc_load_tmp), .ADR_WL(control_unit_1_adr_wl), .ADR_WH(control_unit_1_adr_wh),
    .ADR_RL(control_unit_1_adr_rl), .ADR_RH(control_unit_1_adr_rh), .ADR_LOAD(control_unit_1_adr_load),
    .GPR_WE(control_unit_1_gpr_we), .GPR_ACC_WE(control_unit_1_gpr_acc_we),
    .GPR_OUT_WE(control_unit_1_gpr_out_we), .GPR_RE(control_unit_1_gpr_re),
    .GPR_OUT_RE(control_unit_1_gpr_out_re), .GPR_SP_INC(control_unit_1_gpr_sp_inc),
    .GPR_SP_DEC(control_unit_1_gpr_sp_dec), .ALU_EN(control_unit_1_alu_en),
    .FLAGS_WE(control_unit_1_flags_we), .FLAGS_LOAD(control_unit_1_flags_load),
    .FLAGS_RE(control_unit_1_flags_re), .IR_WE(control_unit_1_ir_we), .RAM_WE(RAM_WE), .RAM_RE(RAM_RE),
    .ADDR_SEL(control_unit_1_addr_sel), .INT(interrupt_service_system_1_interrupt_out),
    .Instruction(instruction_register_1_instruction_out), .flags(flags_register_1_alu_in), .CLK(CLK),
    .CLR(s_r_ff_1_q));
  Multiplexer #(.enable("false"), .select(2), .width(16)) multiplexer_1 (
    .in0(temporary_register_1_address_out), .in1(program_counter_1_address_out),
    .in2(address_register_1_address_out), .in3(register_file_1_stack_pointer_out), .out(Address_Out),
    .sel(control_unit_1_addr_sel));
  // Probe on program_counter_1_data_out
  // Probe on program_counter_1_data_out
  // Probe on program_counter_1_data_out
  // Probe on program_counter_1_data_out
  Interrupt_Service_System interrupt_service_system_1 (
    .Address_Out(interrupt_service_system_1_address_out),
    .Interrupt_Out(interrupt_service_system_1_interrupt_out), .Interrupt_In(INT),
    .INT_ENABLE(control_unit_1_int_enable), .INT_DISABLE(control_unit_1_int_disable), .CLK(CLK),
    .CLR(s_r_ff_1_q), .Data_In(program_counter_1_data_out), .LOW_WE(control_unit_1_iss_wl),
    .HIGH_WE(control_unit_1_iss_wh));
  Temporary_Register temporary_register_1 (
    .Address_Out(temporary_register_1_address_out), .INC(control_unit_1_tmp_inc),
    .Data_In(program_counter_1_data_out), .LOW_WE(control_unit_1_tmp_wl), .LOAD(control_unit_1_tmp_load),
    .FROM_ADR(control_unit_1_tmp_from_adr), .Address_In(address_register_1_address_out),
    .HIGH_WE(control_unit_1_tmp_wh), .CLK(CLK), .CLR(s_r_ff_1_q), .DEC(control_unit_1_tmp_dec));
  Program_Counter program_counter_1 (
    .Data_Out(program_counter_1_data_out), .Address_Out(program_counter_1_address_out),
    .Data_In(program_counter_1_data_out), .ISS_In(interrupt_service_system_1_address_out),
    .TMP_In(temporary_register_1_address_out), .LOW_WE(control_unit_1_pc_wl), .LOAD(control_unit_1_pc_load),
    .LOAD_TMP(control_unit_1_pc_load_tmp), .LOAD_ISS(control_unit_1_pc_load_iss),
    .HIGH_WE(control_unit_1_pc_wh), .CLK(CLK), .CLR(s_r_ff_1_q), .LOW_RE(control_unit_1_pc_rl),
    .HIGH_RE(control_unit_1_pc_rh));
  Address_Register address_register_1 (
    .Data_Out(program_counter_1_data_out), .Address_Out(address_register_1_address_out),
    .Address_In(temporary_register_1_address_out), .Data_In(program_counter_1_data_out),
    .LOAD(control_unit_1_adr_load), .LOW_WE(control_unit_1_adr_wl), .HIGH_WE(control_unit_1_adr_wh),
    .CLK(CLK), .CLR(s_r_ff_1_q), .LOW_RE(control_unit_1_adr_rl), .HIGH_RE(control_unit_1_adr_rh));
  Register_File register_file_1 (
    .Stack_Pointer_Out(register_file_1_stack_pointer_out), .Data_Out(program_counter_1_data_out),
    .ALU_In(register_file_1_alu_in), .SP_INC(control_unit_1_gpr_sp_inc), .SP_DEC(control_unit_1_gpr_sp_dec),
    .CLK(CLK), .CLR(s_r_ff_1_q), .OUT_RE(control_unit_1_gpr_out_re), .RE(control_unit_1_gpr_re),
    .ACC_WE(control_unit_1_gpr_acc_we), .ALU_Out(arithmetic_logic_unit_1_out),
    .OUT_WE(control_unit_1_gpr_out_we), .Data_In(program_counter_1_data_out), .WE(control_unit_1_gpr_we),
    .SEL(control_unit_1_gpr_sel));
  Arithmetic_Logic_Unit arithmetic_logic_unit_1 (
    .Out(arithmetic_logic_unit_1_out), .Flags_Out(arithmetic_logic_unit_1_flags_out),
    .A_In(program_counter_1_data_out), .Enable(control_unit_1_alu_en), .B_In(register_file_1_alu_in),
    .Operation(control_unit_1_alu_op), .Flags_In(flags_register_1_alu_in));
  Flags_Register flags_register_1 (
    .ALU_In(flags_register_1_alu_in), .Data_Out(program_counter_1_data_out),
    .ALU_Out(arithmetic_logic_unit_1_flags_out), .Data_In(program_counter_1_data_out),
    .LOAD(control_unit_1_flags_load), .WE(control_unit_1_flags_we), .CLK(CLK), .CLR(s_r_ff_1_q),
    .RE(control_unit_1_flags_re));
  Instruction_Register instruction_register_1 (
    .Instruction_Out(instruction_register_1_instruction_out), .Data_In(program_counter_1_data_out),
    .WE(control_unit_1_ir_we), .CLK(CLK), .CLR(s_r_ff_1_q));
  assign Data_Out = RAM_WE ? program_counter_1_data_out : 8'bz;  // Controlled_Buffer controlled_buffer_1
  assign program_counter_1_data_out = RAM_RE ? Data_In : 8'bz;  // Controlled_Buffer controlled_buffer_2

  // Notes on the sheet:
  //   Data Bus
endmodule

// GPR
module Register_File (
  input  [2:0] SEL,
  input  [7:0] Data_In,
  input  WE,
  input  ACC_WE,
  input  [7:0] ALU_Out,
  input  OUT_WE,
  input  SP_INC,
  input  SP_DEC,
  input  CLK,
  input  CLR,
  input  OUT_RE,
  input  RE,
  output [7:0] Data_Out,
  output [7:0] ALU_In,
  output [15:0] Stack_Pointer_Out
);

  wire demultiplexer_1_out0, demultiplexer_1_out1, demultiplexer_1_out2, demultiplexer_1_out3,
       demultiplexer_1_out4, demultiplexer_1_out5, demultiplexer_1_out6, demultiplexer_1_out7, or_1_out,
       or_2_out, or_3_out, or_4_out, or_5_out;
  wire [7:0] adder_1_out, bit_extender_1_out, multiplexer_1_out, multiplexer_2_out, multiplexer_3_out, r0_q,
       r1_q, r2_q, r3_q, r4_q, r6_q, xor_1_out;

  assign bit_extender_1_out = {{7{SP_DEC}}, SP_DEC};  // Bit_Extender bit_extender_1
  assign xor_1_out = bit_extender_1_out ^ {8{1'b0}};  // XOR_Gate xor_1, 8 bits wide
  Demultiplexer #(.enable("false"), .select(3)) demultiplexer_1 (
    .out0(demultiplexer_1_out0), .out1(demultiplexer_1_out1), .out2(demultiplexer_1_out2),
    .out3(demultiplexer_1_out3), .out4(demultiplexer_1_out4), .out5(demultiplexer_1_out5),
    .out6(demultiplexer_1_out6), .out7(demultiplexer_1_out7), .in(WE), .sel(SEL));
  Adder adder_1 (.a(Stack_Pointer_Out[7:0]), .b(xor_1_out), .out(adder_1_out), .cin(SP_INC));  // open: cout
  or or_1 (or_1_out, SP_INC, SP_DEC);
  Multiplexer #(.enable("false"), .width(8)) multiplexer_1 (
    .in0(Data_In), .in1(ALU_Out), .out(multiplexer_1_out), .sel(OUT_WE));
  Multiplexer #(.enable("false"), .width(8)) multiplexer_2 (
    .in0(Data_In), .in1(adder_1_out), .out(multiplexer_2_out), .sel(or_1_out));
  Register r0 (.D(Data_In), .en(demultiplexer_1_out0), .clk(CLK), .Q(r0_q), .clr(CLR));
  Register r1 (.D(Data_In), .en(demultiplexer_1_out1), .clk(CLK), .Q(r1_q), .clr(CLR));
  Register r2 (.D(Data_In), .en(demultiplexer_1_out2), .clk(CLK), .Q(r2_q), .clr(CLR));
  Register r3 (.D(Data_In), .en(demultiplexer_1_out3), .clk(CLK), .Q(r3_q), .clr(CLR));
  Register r4 (.D(Data_In), .en(demultiplexer_1_out4), .clk(CLK), .Q(r4_q), .clr(CLR));
  Register r5 (.D(Data_In), .en(or_2_out), .clk(CLK), .Q(ALU_In), .clr(CLR));
  or or_2 (or_2_out, demultiplexer_1_out5, ACC_WE);
  Register r6 (.D(multiplexer_1_out), .en(or_3_out), .clk(CLK), .Q(r6_q), .clr(CLR));
  or or_3 (or_3_out, demultiplexer_1_out6, OUT_WE);
  Register r7 (.D(multiplexer_2_out), .en(or_4_out), .clk(CLK), .Q(Stack_Pointer_Out[7:0]), .clr(CLR));
  or or_4 (or_4_out, demultiplexer_1_out7, or_1_out);
  Multiplexer #(.enable("false"), .select(3), .width(8)) multiplexer_3 (
    .in0(r0_q), .in1(r1_q), .in2(r2_q), .in3(r3_q), .in4(r4_q), .in5(ALU_In), .in6(r6_q),
    .in7(Stack_Pointer_Out[7:0]), .out(multiplexer_3_out), .sel(SEL));
  Multiplexer #(.disabled("Z"), .width(8)) multiplexer_4 (
    .in0(multiplexer_3_out), .in1(r6_q), .out(Data_Out), .sel(OUT_RE), .en(or_5_out));
  or or_5 (or_5_out, OUT_RE, RE);

  assign Stack_Pointer_Out[15:8] = 8'h8;
endmodule

// ALU
module Arithmetic_Logic_Unit (
  input  [7:0] A_In,
  input  Enable,
  input  [7:0] B_In,
  input  [3:0] Operation,
  input  [1:0] Flags_In,
  output [7:0] Out,
  output [1:0] Flags_Out
);

  wire adder_1_cout, and_2_out, demultiplexer_1_out2, demultiplexer_1_out4, demultiplexer_1_out5,
       demultiplexer_1_out6, demultiplexer_1_out7, demultiplexer_1_out15, nor_1_out, or_1_out, or_2_out,
       or_3_out, or_5_out;
  wire [7:0] adder_1_out, and_1_out, bit_extender_1_out, multiplexer_1_out, multiplexer_2_out,
       multiplexer_3_out, multiplexer_4_out, not_1_out, or_4_out, shifter_1_out, shifter_2_out, xor_1_out,
       xor_2_out;

  Multiplexer #(.enable("false"), .width(8)) multiplexer_1 (
    .in0({8{1'b0}}), .in1(A_In), .out(multiplexer_1_out), .sel(Enable));
  Multiplexer #(.enable("false"), .width(8)) multiplexer_2 (
    .in0({8{1'b0}}), .in1(B_In), .out(multiplexer_2_out), .sel(Enable));
  Demultiplexer #(.enable("false"), .select(4)) demultiplexer_1 (
    .out2(demultiplexer_1_out2), .out4(demultiplexer_1_out4), .out5(demultiplexer_1_out5),
    .out6(demultiplexer_1_out6), .out7(demultiplexer_1_out7), .out15(demultiplexer_1_out15), .in(Enable),
    .sel(Operation));  // open: out0, out1, out3, out8, out9, out10, out11, out12, out13, out14
  or or_1 (or_1_out, demultiplexer_1_out4, demultiplexer_1_out15);
  nor nor_1 (nor_1_out, demultiplexer_1_out7, demultiplexer_1_out6);
  Multiplexer #(.width(8)) multiplexer_3 (
    .in0(multiplexer_2_out), .in1(multiplexer_1_out), .out(multiplexer_3_out), .sel(demultiplexer_1_out5),
    .en(nor_1_out));
  or or_2 (or_2_out, demultiplexer_1_out7, demultiplexer_1_out5, or_1_out);
  or or_3 (or_3_out, demultiplexer_1_out7, or_1_out);
  assign and_1_out = multiplexer_1_out & multiplexer_2_out;  // AND_Gate and_1, 8 bits wide
  assign or_4_out = multiplexer_1_out | multiplexer_2_out;  // OR_Gate or_4, 8 bits wide
  assign not_1_out = ~multiplexer_1_out;  // NOT_Gate not_1, 8 bits wide
  and and_2 (and_2_out, Flags_In[1], demultiplexer_1_out2);
  assign bit_extender_1_out = {{7{or_2_out}}, or_2_out};  // Bit_Extender bit_extender_1
  assign xor_1_out = multiplexer_1_out ^ multiplexer_2_out;  // XOR_Gate xor_1, 8 bits wide
  Shifter #(.shift("lr")) shifter_1 (.in(multiplexer_1_out), .\dist (multiplexer_2_out[2:0]), .out(shifter_1_out));
  Shifter shifter_2 (.in(multiplexer_1_out), .\dist (multiplexer_2_out[2:0]), .out(shifter_2_out));
  or or_5 (or_5_out, and_2_out, or_1_out, demultiplexer_1_out5, demultiplexer_1_out6);
  Multiplexer #(.enable("false"), .width(8)) multiplexer_4 (
    .in0(multiplexer_1_out), .in1({8{1'b0}}), .out(multiplexer_4_out), .sel(demultiplexer_1_out5));
  Adder adder_1 (.a(multiplexer_4_out), .b(xor_2_out), .out(adder_1_out), .cin(or_5_out), .cout(adder_1_cout));
  assign xor_2_out = multiplexer_3_out ^ bit_extender_1_out;  // XOR_Gate xor_2, 8 bits wide
  xor xor_3 (Flags_Out[1], or_3_out, adder_1_cout);
  Multiplexer #(.enable("false"), .select(4), .width(8)) multiplexer_5 (
    .in0({8{1'b0}}), .in1({8{1'b0}}), .in2(adder_1_out), .in3(adder_1_out), .in4(adder_1_out),
    .in5(adder_1_out), .in6(adder_1_out), .in7(adder_1_out), .in8(multiplexer_1_out), .in9(and_1_out),
    .in10(or_4_out), .in11(not_1_out), .in12(xor_1_out), .in13(shifter_1_out), .in14(shifter_2_out),
    .in15(adder_1_out), .out(Out), .sel(Operation));
  Comparator #(.mode("unsigned")) comparator_1 (.a(Out), .b({8{1'b0}}), .eq(Flags_Out[0]));  // open: gt, lt
endmodule

// FLAGS
module Flags_Register (
  input  [1:0] ALU_Out,
  input  [7:0] Data_In,
  input  LOAD,
  input  WE,
  input  CLK,
  input  CLR,
  input  RE,
  output [1:0] ALU_In,
  output [7:0] Data_Out
);

  wire [1:0] multiplexer_1_out;

  Multiplexer #(.enable("false"), .width(2)) multiplexer_1 (
    .in0(ALU_Out), .in1(Data_In[1:0]), .out(multiplexer_1_out), .sel(LOAD));
  Register #(.width(2)) flags (.D(multiplexer_1_out), .en(WE), .clk(CLK), .Q(ALU_In), .clr(CLR));
  assign Data_Out = RE ? {{6{1'b0}}, ALU_In} : 8'bz;  // Controlled_Buffer controlled_buffer_1
endmodule

// ADR
module Address_Register (
  input  [7:0] Data_In,
  input  LOW_WE,
  input  LOAD,
  input  [15:0] Address_In,
  input  HIGH_WE,
  input  CLK,
  input  CLR,
  input  LOW_RE,
  input  HIGH_RE,
  output [7:0] Data_Out,
  output [15:0] Address_Out
);

  wire or_1_out;
  wire [7:0] multiplexer_1_out, multiplexer_2_out;

  Multiplexer #(.enable("false"), .width(8)) multiplexer_1 (
    .in0(Data_In), .in1(Address_In[7:0]), .out(multiplexer_1_out), .sel(LOAD));
  Multiplexer #(.enable("false"), .width(8)) multiplexer_2 (
    .in0(Data_In), .in1(Address_In[15:8]), .out(multiplexer_2_out), .sel(LOAD));
  Register low (.D(multiplexer_1_out), .en(LOW_WE), .clk(CLK), .Q(Address_Out[7:0]), .clr(CLR));
  Register high (.D(multiplexer_2_out), .en(HIGH_WE), .clk(CLK), .Q(Address_Out[15:8]), .clr(CLR));
  or or_1 (or_1_out, LOW_RE, HIGH_RE);
  Multiplexer #(.disabled("Z"), .width(8)) multiplexer_3 (
    .in0(Address_Out[7:0]), .in1(Address_Out[15:8]), .out(Data_Out), .sel(HIGH_RE), .en(or_1_out));
endmodule

// PC
module Program_Counter (
  input  [7:0] Data_In,
  input  [15:0] ISS_In,
  input  [15:0] TMP_In,
  input  LOW_WE,
  input  LOAD,
  input  LOAD_TMP,
  input  LOAD_ISS,
  input  HIGH_WE,
  input  CLK,
  input  CLR,
  input  LOW_RE,
  input  HIGH_RE,
  output [7:0] Data_Out,
  output [15:0] Address_Out
);

  wire adder_1_cout, not_1_out, or_1_out, or_2_out, or_3_out;
  wire [7:0] adder_1_out, adder_2_out, multiplexer_2_out, multiplexer_3_out, multiplexer_4_out,
       multiplexer_5_out;
  wire [15:0] multiplexer_1_out;

  Multiplexer #(.enable("false"), .width(16)) multiplexer_1 (
    .in0(ISS_In), .in1(TMP_In), .out(multiplexer_1_out), .sel(LOAD_TMP));
  or or_1 (or_1_out, LOAD_TMP, LOAD_ISS);
  not not_1 (not_1_out, or_2_out);
  Adder adder_1 (.a(Address_Out[7:0]), .b({8{1'b0}}), .out(adder_1_out), .cin(not_1_out), .cout(adder_1_cout));
  Adder adder_2 (.a(Address_Out[15:8]), .b({8{1'b0}}), .out(adder_2_out), .cin(adder_1_cout));  // open: cout
  Multiplexer #(.enable("false"), .width(8)) multiplexer_2 (
    .in0(Data_In), .in1(multiplexer_1_out[7:0]), .out(multiplexer_2_out), .sel(or_1_out));
  or or_2 (or_2_out, LOAD, or_1_out);
  Multiplexer #(.enable("false"), .width(8)) multiplexer_3 (
    .in0(Data_In), .in1(multiplexer_1_out[15:8]), .out(multiplexer_3_out), .sel(or_1_out));
  Multiplexer #(.enable("false"), .width(8)) multiplexer_4 (
    .in0(adder_1_out), .in1(multiplexer_2_out), .out(multiplexer_4_out), .sel(or_2_out));
  Register low (.D(multiplexer_4_out), .en(LOW_WE), .clk(CLK), .Q(Address_Out[7:0]), .clr(CLR));
  Register high (.D(multiplexer_5_out), .en(HIGH_WE), .clk(CLK), .Q(Address_Out[15:8]), .clr(CLR));
  Multiplexer #(.enable("false"), .width(8)) multiplexer_5 (
    .in0(adder_2_out), .in1(multiplexer_3_out), .out(multiplexer_5_out), .sel(or_2_out));
  or or_3 (or_3_out, LOW_RE, HIGH_RE);
  Multiplexer #(.disabled("Z"), .width(8)) multiplexer_6 (
    .in0(Address_Out[7:0]), .in1(Address_Out[15:8]), .out(Data_Out), .sel(HIGH_RE), .en(or_3_out));
endmodule

// TMP
module Temporary_Register (
  input  INC,
  input  [7:0] Data_In,
  input  LOW_WE,
  input  LOAD,
  input  FROM_ADR,
  input  [15:0] Address_In,
  input  HIGH_WE,
  input  CLK,
  input  CLR,
  input  DEC,
  output [15:0] Address_Out
);

  wire adder_1_cout;
  wire [7:0] adder_1_out, adder_2_out, bit_extender_1_out, multiplexer_1_out, multiplexer_2_out,
       multiplexer_3_out, multiplexer_4_out;

  assign bit_extender_1_out = {{7{DEC}}, DEC};  // Bit_Extender bit_extender_1
  Multiplexer #(.enable("false"), .width(8)) multiplexer_1 (
    .in0(Data_In), .in1(Address_In[7:0]), .out(multiplexer_1_out), .sel(FROM_ADR));
  Multiplexer #(.enable("false"), .width(8)) multiplexer_2 (
    .in0(Data_In), .in1(Address_In[15:8]), .out(multiplexer_2_out), .sel(FROM_ADR));
  Adder adder_1 (.a(Address_Out[7:0]), .b(bit_extender_1_out), .out(adder_1_out), .cin(INC), .cout(adder_1_cout));
  Multiplexer #(.enable("false"), .width(8)) multiplexer_3 (
    .in0(adder_1_out), .in1(multiplexer_1_out), .out(multiplexer_3_out), .sel(LOAD));
  Adder adder_2 (.a(Address_Out[15:8]), .b(bit_extender_1_out), .out(adder_2_out), .cin(adder_1_cout));  // open: cout
  Multiplexer #(.enable("false"), .width(8)) multiplexer_4 (
    .in0(adder_2_out), .in1(multiplexer_2_out), .out(multiplexer_4_out), .sel(LOAD));
  Register low (.D(multiplexer_3_out), .en(LOW_WE), .clk(CLK), .Q(Address_Out[7:0]), .clr(CLR));
  Register high (.D(multiplexer_4_out), .en(HIGH_WE), .clk(CLK), .Q(Address_Out[15:8]), .clr(CLR));
endmodule

// ISS
module Interrupt_Service_System (
  input  [7:0] Data_In,
  input  LOW_WE,
  input  HIGH_WE,
  input  Interrupt_In,
  input  INT_ENABLE,
  input  INT_DISABLE,
  input  CLK,
  input  CLR,
  output [15:0] Address_Out,
  output Interrupt_Out
);

  wire enabled_q, or_1_out, triggered_q;

  or or_1 (or_1_out, INT_ENABLE, INT_DISABLE);
  D_Flip_Flop triggered (.D(Interrupt_In), .clk(CLK), .Q(triggered_q), .reset(CLR));  // open: Qn, preset
  Register low (.D(Data_In), .en(LOW_WE), .clk(CLK), .Q(Address_Out[7:0]), .clr(CLR));
  Register high (.D(Data_In), .en(HIGH_WE), .clk(CLK), .Q(Address_Out[15:8]), .clr(CLR));
  Register #(.width(1)) enabled (.D(INT_ENABLE), .en(or_1_out), .clk(CLK), .Q(enabled_q), .clr(CLR));
  and and_1 (Interrupt_Out, triggered_q, enabled_q);
endmodule

// IR
module Instruction_Register (
  input  [7:0] Data_In,
  input  WE,
  input  CLK,
  input  CLR,
  output [7:0] Instruction_Out
);

  Register instruction (.D(Data_In), .en(WE), .clk(CLK), .Q(Instruction_Out), .clr(CLR));
endmodule

module Control_Unit (
  input  CLK,
  input  CLR,
  input  INT,
  input  [7:0] Instruction,
  input  [1:0] flags,
  output ISS_WL,
  output ISS_WH,
  output INT_ENABLE,
  output INT_DISABLE,
  output TMP_WL,
  output TMP_WH,
  output TMP_LOAD,
  output TMP_FROM_ADR,
  output TMP_INC,
  output TMP_DEC,
  output PC_WL,
  output PC_WH,
  output PC_RL,
  output PC_RH,
  output PC_LOAD,
  output PC_LOAD_ISS,
  output PC_LOAD_TMP,
  output ADR_WL,
  output ADR_WH,
  output ADR_RL,
  output ADR_RH,
  output ADR_LOAD,
  output GPR_WE,
  output GPR_ACC_WE,
  output GPR_OUT_WE,
  output GPR_RE,
  output GPR_OUT_RE,
  output GPR_SP_INC,
  output GPR_SP_DEC,
  output ALU_EN,
  output FLAGS_WE,
  output FLAGS_LOAD,
  output FLAGS_RE,
  output IR_WE,
  output RAM_WE,
  output RAM_RE,
  output [1:0] ADDR_SEL,
  output [2:0] GPR_SEL,
  output [3:0] ALU_OP
);

  wire and_1_out, and_2_out, and_3_out, comparator_1_eq, comparator_2_lt, comparator_3_eq, comparator_4_gt,
       Entering_ISR_q, or_1_out;
  wire [2:0] stepper_1_step;
  wire [31:0] and_4_out, and_5_out, and_6_out, and_7_out, and_8_out, and_9_out, and_10_out, and_11_out,
       bit_extender_1_out, bit_extender_2_out, bit_extender_3_out, bit_extender_4_out,
       Interrupt_Responder_p1, Interrupt_Responder_p2, Jump_Instruction_p1, Jump_Instruction_p2,
       One_Operand_Instructions_p1, One_Operand_Instructions_p2, Zero_Operand_Instructions_p1,
       Zero_Operand_Instructions_p2;
  wire [31:6] or_3_out;

  Comparator #(.mode("unsigned"), .width(3)) comparator_1 (
    .a(stepper_1_step), .b(3'b000), .eq(comparator_1_eq));  // open: gt, lt
  D_Flip_Flop Entering_ISR (.D(INT), .clk(comparator_1_eq), .Q(Entering_ISR_q), .reset(CLR));  // open: Qn, preset
  or or_1 (or_1_out, or_3_out[6], CLR);
  // ROM #(.addrWidth(4), .dataWidth(32), .line("dual")) Interrupt_Responder: pin names not known; wires that end beside it: Interrupt_Responder_p1, Interrupt_Responder_p2
  // ROM #(.addrWidth(9), .dataWidth(32), .line("dual")) Zero_Operand_Instructions: pin names not known; wires that end beside it: Zero_Operand_Instructions_p1, Zero_Operand_Instructions_p2
  // ROM #(.addrWidth(9), .dataWidth(32), .line("dual")) Jump_Instruction: pin names not known; wires that end beside it: Jump_Instruction_p1, Jump_Instruction_p2
  // ROM #(.addrWidth(9), .dataWidth(32), .line("dual")) One_Operand_Instructions: pin names not known; wires that end beside it: One_Operand_Instructions_p1, One_Operand_Instructions_p2
  Stepper stepper_1 (.Step(stepper_1_step), .Clk(CLK), .Clr(or_1_out));
  Comparator #(.mode("unsigned")) comparator_2 (.a(Instruction), .b(8'h18), .lt(comparator_2_lt));  // open: gt, eq
  Comparator #(.mode("unsigned"), .width(5)) comparator_3 (
    .a(Instruction[7:3]), .b(5'b00011), .eq(comparator_3_eq));  // open: gt, lt
  Comparator #(.mode("unsigned"), .width(5)) comparator_4 (
    .a(Instruction[7:3]), .b(5'b00011), .gt(comparator_4_gt));  // open: eq, lt
  assign bit_extender_1_out = {{31{Entering_ISR_q}}, Entering_ISR_q};  // Bit_Extender bit_extender_1
  assign bit_extender_2_out = {{31{and_1_out}}, and_1_out};  // Bit_Extender bit_extender_2
  and and_1 (and_1_out, ~Entering_ISR_q, comparator_2_lt);  // AND_Gate
  assign bit_extender_3_out = {{31{and_2_out}}, and_2_out};  // Bit_Extender bit_extender_3
  and and_2 (and_2_out, ~Entering_ISR_q, comparator_3_eq);  // AND_Gate
  assign bit_extender_4_out = {{31{and_3_out}}, and_3_out};  // Bit_Extender bit_extender_4
  and and_3 (and_3_out, ~Entering_ISR_q, comparator_4_gt);  // AND_Gate
  assign and_4_out = Interrupt_Responder_p1 & bit_extender_1_out;  // AND_Gate and_4, 32 bits wide
  assign and_5_out = Interrupt_Responder_p2 & bit_extender_1_out;  // AND_Gate and_5, 32 bits wide
  assign and_6_out = Zero_Operand_Instructions_p1 & bit_extender_2_out;  // AND_Gate and_6, 32 bits wide
  assign and_7_out = Zero_Operand_Instructions_p2 & bit_extender_2_out;  // AND_Gate and_7, 32 bits wide
  assign and_8_out = Jump_Instruction_p1 & bit_extender_3_out;  // AND_Gate and_8, 32 bits wide
  assign and_9_out = Jump_Instruction_p2 & bit_extender_3_out;  // AND_Gate and_9, 32 bits wide
  assign and_10_out = One_Operand_Instructions_p1 & bit_extender_4_out;  // AND_Gate and_10, 32 bits wide
  assign and_11_out = One_Operand_Instructions_p2 & bit_extender_4_out;  // AND_Gate and_11, 32 bits wide
  assign {FLAGS_LOAD, FLAGS_WE, ALU_EN, GPR_SP_DEC, GPR_SP_INC, GPR_OUT_RE, GPR_RE, GPR_OUT_WE, GPR_ACC_WE, GPR_WE, ADR_LOAD, ADR_RH, ADR_RL, ADR_WH, ADR_WL, PC_LOAD_TMP, PC_LOAD_ISS, PC_LOAD, PC_RH, PC_RL, PC_WH, PC_WL, TMP_DEC, TMP_INC, TMP_FROM_ADR, TMP_LOAD, TMP_WH, TMP_WL, INT_DISABLE, INT_ENABLE, ISS_WH, ISS_WL} = and_4_out | and_6_out | and_8_out | and_10_out;  // OR_Gate or_2, 32 bits wide
  assign {or_3_out, ADDR_SEL, RAM_RE, RAM_WE, IR_WE, FLAGS_RE} = and_5_out | and_7_out | and_9_out | and_11_out;  // OR_Gate or_3, 32 bits wide

  assign ALU_OP = Instruction[6:3];
  assign GPR_SEL = Instruction[2:0];

  // Notes on the sheet:
  //   contents of Interrupt_Responder (hex, n*v repeats v):
  //   10000008 0 10002000 34 10001000 34 8c00 35 0 40
  //   contents of Zero_Operand_Instructions (hex, n*v repeats v):
  //   c00 1a 0 10 0 40 10*0 c00 1a c01 18 c02 18 0 40 8*0 c00 1a 8 10 0 40 10*0 c00 1a 4 10 0 40 10*0 c00
  //   1a c8000004 38 8004400 38 8004800 38 0 40 6*0 c00 1a c50 18 10000c60 18 10002000 34 11000 34 0 40
  //   4*0 c00 1a 8004400 38 8004800 38 0 40 8*0 c00 1a 10000000 10 0 35 0 40 8*0 c00 1a c8000000 38 0 40
  //   10*0 c00 1a 20c00 18 0 40 10*0 c00 1a 40c00 18 0 40 10*0 c00 1a 20c00 18 40c00 18 0 40 8*0 c00 1a
  //   c50 18 c60 18 20130 8 40000 8 0 40 4*0 c00 1a f0 10 20130 8 40000 8 0 40 6*0 c00 1a 8020000 38
  //   8040000 38 0 40 8*0 c00 1a c50 18 c60 18 80130 4 100000 4 0 40 4*0 c00 1a f0 10 80130 4 100000 4 0
  //   40 6*0 c00 1a 10000000 10 10080000 34 100000 34 0 40 7*0 40 0 40 12*0 c00 1a 14*0 c00 1a 14*0 c00 1a
  //   14*0 c00 1a 14*0 c00 1a
  //   contents of Jump_Instruction (hex, n*v repeats v):
  //   c00 1a c50 18 c60 18 10c00 10 0 40 6*0 c00 1a c50 18 c60 18 10c00 10 0 40 6*0 c00 1a c50 18 c60 18
  //   10c00 10 0 40 6*0 c00 1a c50 18 c60 18 10c00 10 0 40 6*0 c00 1a c50 18 c60 18 10c00 10 0 40 6*0 c00
  //   1a c50 18 c60 18 0 10 0 40 6*0 c00 1a c50 18 c60 18 10c00 10 0 40 6*0 c00 1a c50 18 c60 18 0 10 0 40
  //   6*0 c00 1a c50 18 c60 18 0 10 0 40 6*0 c00 1a c50 18 c60 18 10c00 10 0 40 6*0 c00 1a c50 18 c60 18 0
  //   10 0 40 6*0 c00 1a c50 18 c60 18 10c00 10 0 40 6*0 c00 1a c50 18 c60 18 0 10 0 40 6*0 c00 1a c50 18
  //   c60 18 0 10 0 40 6*0 c00 1a c50 18 c60 18 10c00 10 0 40 6*0 c00 1a c50 18 c60 18 10c00 10 0 40 6*0
  //   c00 1a c50 18 c60 18 10c00 10 0 40 6*0 c00 1a c50 18 c60 18 10c00 10 0 40 6*0 c00 1a c50 18 c60 18 0
  //   10 0 40 6*0 c00 1a c50 18 c60 18 0 10 0 40 6*0 c00 1a c50 18 c60 18 10c00 10 0 40 6*0 c00 1a c50 18
  //   c60 18 0 10 0 40 6*0 c00 1a c50 18 c60 18 0 10 0 40 6*0 c00 1a c50 18 c60 18 0 10 0 40 6*0 c00 1a
  //   c50 18 c60 18 0 10 0 40 6*0 c00 1a c50 18 c60 18 10c00 10 0 40 6*0 c00 1a c50 18 c60 18 10c00 10 0
  //   40 6*0 c00 1a c50 18 c60 18 0 10 0 40 6*0 c00 1a 14*0 c00 1a 14*0 c00 1a 14*0 c00 1a
  //   contents of One_Operand_Instructions (hex, n*v repeats v):
  //   64*0 c00 1a 400c00 18 0 40 10*0 c00 1a c50 18 c60 18 400000 8 0 40 6*0 c00 1a 400000 28 0 40 10*0
  //   c00 1a 8400000 38 0 40 10*0 c00 1a c50 18 c60 18 2000000 4 0 40 6*0 c00 1a 2000000 24 0 40 10*0 c00
  //   1a 10000000 10 2000000 34 0 40 8*0 c00 1a 2800000 10 0 40 10*0 c00 1a 4400000 10 0 40 10*0 c00 1a
  //   480000 10 0 40 10*0 c00 1a 500000 10 0 40 10*0 c00 1a 2020000 10 0 40 10*0 c00 1a 2040000 10 0 40
  //   10*0 c00 1a 14*0 c00 1a 63000000 10 0 40 10*0 c00 1a 63000000 10 0 40 10*0 c00 1a 63000000 10 0 40
  //   10*0 c00 1a 63000000 10 0 40 10*0 c00 1a 63000000 10 0 40 10*0 c00 1a 63000000 10 0 40 10*0 c00 1a
  //   62000000 10 0 40 10*0 c00 1a 63000000 10 0 40 10*0 c00 1a 63000000 10 0 40 10*0 c00 1a 63000000 10 0
  //   40 10*0 c00 1a 63000000 10 0 40 10*0 c00 1a 63000000 10 0 40 10*0 c00 1a 63000000 10 0 40 10*0 c00
  //   1a 62000000 10 0 40
endmodule

module Stepper (
  input  Clk,
  input  Clr,
  output [2:0] Step
);

  wire [2:0] adder_1_out;

  Adder #(.width(3)) adder_1 (.a(Step), .b(3'b000), .out(adder_1_out), .cin(1'b1));  // open: cout
  Register #(.width(3)) u_step (.D(adder_1_out), .en(1'b1), .clk(Clk), .Q(Step), .clr(Clr));
endmodule
