// Logisim project Demo8 No Roms.circ as structural Verilog
module Control_Unit (
  input  CLR,
  input  CLK_plus,
  input  INT_In,
  input  [1:0] Flags_Out,
  input  [7:0] Instruction,
  output GPR_WE,
  output ACC_WE,
  output OUT_WE,
  output GPR_RE,
  output OUT_RE,
  output SP_INC,
  output SP_DEC,
  output ADR_WL,
  output ADR_WH,
  output ADR_RL,
  output ADR_RH,
  output ADR_LOAD,
  output RAM_WE,
  output RAM_RE,
  output TMP_WL,
  output TMP_WH,
  output TMP_LOAD,
  output TMP_LOAD_ADR,
  output TMP_INC,
  output TMP_DEC,
  output ALU_Enable,
  output [3:0] out_27,
  output INT_WL,
  output INT_WH,
  output INT_Enable,
  output INT_Disable,
  output Flags_WE,
  output Flags_Load,
  output Flags_RE,
  output [1:0] ADDR_SEL,
  output IR_WE,
  output PC_LD_TMP,
  output PC_LD_ISS,
  output PC_LD,
  output PC_RH,
  output PC_RL,
  output PC_WH,
  output PC_WL
);

  wire and_1_out, and_2_out, and_3_out, and_4_out, d_ff_1_q, d_ff_2_q, d_ff_3_q, d_ff_5_q, d_ff_6_q,
       multiplexer_1_out, multiplexer_2_out, multiplexer_3_out, multiplexer_4_out, multiplexer_5_out,
       nand_1_out, nand_2_out, nand_3_out, nand_4_out, nand_5_out, nand_6_out, nand_8_out, nand_9_out,
       nand_10_out, nand_12_out, nand_13_out, nand_16_out, nand_17_out, nand_18_out, nand_19_out,
       nand_20_out, nand_21_out, nand_22_out, nand_23_out, nand_24_out, nand_25_out, nand_26_out,
       nand_27_out, nand_28_out, nand_29_out, nand_30_out, nand_32_out, nand_33_out, nand_35_out,
       nand_36_out, nand_37_out, nand_38_out, nand_39_out, nand_40_out, nand_41_out, nand_42_out,
       nand_43_out, nand_44_out, nand_45_out, nand_46_out, nand_47_out, nand_48_out, nand_49_out,
       nand_50_out, nand_51_out, nand_52_out, nand_53_out, nand_54_out, nand_55_out, nand_56_out,
       nand_57_out, nand_58_out, nand_59_out, nand_60_out, nand_61_out, nand_62_out, nand_63_out,
       nand_64_out, nand_65_out, nand_66_out, nand_67_out, nand_68_out, nand_69_out, nand_70_out,
       nand_71_out, nand_72_out, nand_75_out, nand_76_out, nand_77_out, nand_78_out, nand_79_out,
       nand_80_out, nand_81_out, nand_82_out, nand_83_out, nand_84_out, nand_85_out, nand_86_out,
       nand_87_out, nand_88_out, nor_1_out, nor_2_out, nor_3_out, nor_4_out, nor_5_out, nor_6_out, nor_7_out,
       nor_8_out, nor_9_out, nor_10_out, nor_11_out, nor_12_out, nor_13_out, nor_14_out, nor_15_out,
       nor_16_out, nor_17_out, nor_18_out, nor_19_out, nor_20_out, nor_21_out, nor_22_out, nor_23_out,
       nor_24_out, nor_25_out, nor_26_out, nor_27_out, nor_28_out, nor_29_out, nor_30_out, nor_31_out,
       nor_32_out, nor_33_out, nor_34_out, nor_35_out, nor_36_out, nor_37_out, nor_38_out, nor_39_out,
       nor_40_out, nor_41_out, nor_42_out, nor_43_out, nor_44_out, nor_45_out, nor_46_out, nor_47_out,
       nor_48_out, nor_49_out, nor_50_out, nor_51_out, nor_52_out, nor_53_out, nor_54_out, nor_55_out,
       nor_56_out, nor_57_out, nor_58_out, nor_59_out, nor_60_out, nor_61_out, nor_62_out, nor_63_out,
       nor_64_out, nor_65_out, nor_66_out, nor_67_out, nor_68_out, nor_69_out, nor_70_out, nor_71_out,
       nor_72_out, nor_73_out, nor_74_out, nor_75_out, not_1_out, not_2_out, not_4_out, not_5_out, not_6_out,
       not_7_out, not_8_out, not_9_out, not_10_out, not_11_out, not_12_out, or_1_out, or_2_out, or_3_out,
       or_4_out, or_5_out, or_6_out, or_7_out, or_8_out, or_9_out, xor_1_out;

  xor xor_1 (xor_1_out, Flags_Out[1], Flags_Out[0]);
  nand nand_1 (nand_1_out, xor_1_out, Flags_Out[1], nor_45_out);
  nand nand_2 (nand_2_out, nand_1_out, nand_6_out, nand_5_out, nand_8_out);
  nand nand_3 (nand_3_out, nor_67_out, or_1_out);
  or or_1 (or_1_out, d_ff_2_q, Flags_Out[1]);
  nand nand_4 (nand_4_out, nor_69_out, or_2_out);
  or or_2 (or_2_out, d_ff_3_q, Flags_Out[1]);
  not not_1 (not_1_out, Flags_Out[1]);
  nand nand_5 (nand_5_out, not_1_out, Flags_Out[1], nor_49_out);
  nand nand_6 (nand_6_out, Flags_Out[1], nor_46_out, not_2_out, not_1_out);
  nand nand_7 (PC_LD, nand_3_out, nand_4_out);
  nand nand_8 (nand_8_out, Flags_Out[1], Flags_Out[1], nor_50_out);
  nand nand_9 (nand_9_out, Flags_Out[0], Flags_Out[1], nor_52_out);
  nand nand_10 (nand_10_out, nand_9_out, nand_12_out, nand_13_out);
  nor nor_1 (nor_1_out, nand_2_out, nand_10_out);
  nand nand_11 (PC_LD_TMP, nor_1_out, nand_38_out);
  not not_2 (not_2_out, Flags_Out[0]);
  nand nand_12 (nand_12_out, not_2_out, Flags_Out[1], nor_53_out);
  nand nand_13 (nand_13_out, Flags_Out[1], nor_54_out);
  not not_3 (PC_LD_ISS, nand_37_out);
  and and_1 (and_1_out, nor_1_out, nor_2_out);
  nor nor_2 (nor_2_out, nand_16_out, nand_17_out, nand_18_out);
  and and_2 (and_2_out, nor_1_out, nor_2_out);
  nand nand_14 (PC_WH, and_1_out, nand_38_out, nand_37_out, nand_59_out);
  nand nand_15 (PC_WL, and_2_out, nand_38_out, nand_37_out, nand_59_out);
  nand nand_16 (nand_16_out, nand_19_out, nand_20_out, nand_21_out, nand_22_out);
  nand nand_17 (nand_17_out, nand_23_out, nand_24_out, nand_25_out, nand_26_out);
  nand nand_18 (nand_18_out, nand_27_out, nand_28_out, nand_29_out);
  nand nand_19 (nand_19_out, or_3_out, nor_72_out);
  nand nand_20 (nand_20_out, or_3_out, nor_68_out);
  nand nand_21 (nand_21_out, nor_64_out, d_ff_2_q);
  nand nand_22 (nand_22_out, nor_63_out, d_ff_2_q);
  nand nand_23 (nand_23_out, or_3_out, nor_62_out);
  nand nand_24 (nand_24_out, or_3_out, nor_61_out);
  nand nand_25 (nand_25_out, or_3_out, nor_58_out);
  nand nand_26 (nand_26_out, or_3_out, nand_30_out);
  nand nand_27 (nand_27_out, nor_40_out, d_ff_2_q);
  nand nand_28 (nand_28_out, or_3_out, nor_37_out);
  nand nand_29 (nand_29_out, or_3_out, nor_32_out);
  or or_3 (or_3_out, d_ff_2_q, d_ff_3_q);
  nand nand_30 (nand_30_out, nor_3_out, nor_4_out);
  nor nor_3 (nor_3_out, nor_54_out, nor_53_out, nor_52_out, nor_50_out);
  nor nor_4 (nor_4_out, nor_49_out, nor_46_out, nor_45_out);
  nor nor_5 (nor_5_out, nand_39_out, nand_47_out);
  nor nor_6 (nor_6_out, nand_39_out, nand_48_out);
  nand nand_31 (PC_RH, nand_32_out, nand_33_out);
  nand nand_32 (nand_32_out, d_ff_6_q, d_ff_2_q);
  nand nand_33 (nand_33_out, Flags_Out[1], nor_68_out);
  D_Flip_Flop d_ff_1 (.D(multiplexer_1_out), .clk(CLK_plus), .Q(d_ff_1_q), .preset(CLR));  // open: Qn, reset
  Multiplexer #(.enable("false")) multiplexer_1 (
    .in0(d_ff_5_q), .in1(d_ff_1_q), .out(multiplexer_1_out), .sel(and_3_out));
  and and_3 (and_3_out, d_ff_2_q, nor_55_out);
  nor nor_7 (nor_7_out, nand_39_out, nand_49_out);
  nor nor_8 (nor_8_out, nand_39_out, nand_50_out);
  nand nand_34 (PC_RL, nand_35_out, nand_36_out);
  nand nand_35 (nand_35_out, d_ff_6_q, d_ff_3_q);
  nand nand_36 (nand_36_out, d_ff_5_q, nor_68_out);
  nor nor_9 (nor_9_out, nand_40_out, nand_47_out);
  nor nor_10 (nor_10_out, nand_40_out, nand_48_out);
  nand nand_37 (nand_37_out, d_ff_6_q, Flags_Out[1]);
  nand nand_38 (nand_38_out, d_ff_5_q, nor_68_out);
  D_Flip_Flop d_ff_2 (.D(multiplexer_2_out), .clk(CLK_plus), .Q(d_ff_2_q), .reset(CLR));  // open: Qn, preset
  Multiplexer #(.enable("false")) multiplexer_2 (
    .in0(d_ff_1_q), .in1(d_ff_2_q), .out(multiplexer_2_out), .sel(and_3_out));
  nor nor_11 (nor_11_out, nand_40_out, nand_49_out);
  nor nor_12 (nor_12_out, nand_40_out, nand_50_out);
  Multiplexer #(.enable("false")) multiplexer_3 (
    .in0(d_ff_2_q), .in1(d_ff_3_q), .out(multiplexer_3_out), .sel(and_3_out));
  nor nor_13 (nor_13_out, nand_41_out, nand_47_out);
  nor nor_14 (nor_14_out, nand_41_out, nand_48_out);
  D_Flip_Flop d_ff_3 (.D(multiplexer_3_out), .clk(CLK_plus), .Q(d_ff_3_q), .reset(CLR));  // open: Qn, preset
  nor nor_15 (nor_15_out, nand_41_out, nand_49_out);
  nor nor_16 (nor_16_out, nand_41_out, nand_50_out);
  D_Flip_Flop d_ff_4 (.D(multiplexer_4_out), .clk(CLK_plus), .Q(Flags_Out[1]), .reset(CLR));  // open: Qn, preset
  Multiplexer #(.enable("false")) multiplexer_4 (
    .in0(d_ff_3_q), .in1(Flags_Out[1]), .out(multiplexer_4_out), .sel(and_3_out));
  nor nor_17 (nor_17_out, nand_42_out, nand_47_out);
  nor nor_18 (nor_18_out, nand_42_out, nand_48_out);
  nor nor_19 (nor_19_out, nand_42_out, nand_50_out);
  nor nor_20 (nor_20_out, nand_43_out, nand_47_out);
  nand nand_39 (nand_39_out, nor_23_out, nor_27_out, nor_31_out);
  D_Flip_Flop d_ff_5 (.D(multiplexer_5_out), .clk(CLK_plus), .Q(d_ff_5_q), .reset(CLR));  // open: Qn, preset
  Multiplexer #(.enable("false")) multiplexer_5 (
    .in0(Flags_Out[1]), .in1(d_ff_5_q), .out(multiplexer_5_out), .sel(and_3_out));
  nor nor_21 (nor_21_out, nand_43_out, nand_48_out);
  nor nor_22 (nor_22_out, nand_43_out, nand_49_out);
  nand nand_40 (nand_40_out, nor_23_out, nor_27_out, nor_34_out);
  nand nand_41 (nand_41_out, nor_23_out, nor_30_out, nor_31_out);
  nor nor_23 (nor_23_out, not_4_out, d_ff_6_q);
  not not_4 (not_4_out, Instruction[7]);
  nor nor_24 (nor_24_out, nand_43_out, nand_50_out);
  nor nor_25 (nor_25_out, nand_44_out, nand_47_out);
  nand nand_42 (nand_42_out, nor_23_out, nor_30_out, nor_34_out);
  nand nand_43 (nand_43_out, nor_26_out, nor_27_out, nor_31_out);
  nor nor_26 (nor_26_out, Instruction[7], d_ff_6_q);
  nor nor_27 (nor_27_out, not_5_out, d_ff_6_q);
  not not_5 (not_5_out, Instruction[6]);
  nor nor_28 (nor_28_out, nand_44_out, nand_48_out);
  nor nor_29 (nor_29_out, nand_44_out, nand_49_out);
  nand nand_44 (nand_44_out, nor_26_out, nor_27_out, nor_34_out);
  nand nand_45 (nand_45_out, nor_26_out, nor_30_out, nor_31_out);
  nor nor_30 (nor_30_out, Instruction[6], d_ff_6_q);
  nor nor_31 (nor_31_out, not_6_out, d_ff_6_q);
  not not_6 (not_6_out, Instruction[5]);
  nor nor_32 (nor_32_out, nand_44_out, nand_50_out);
  nor nor_33 (nor_33_out, nand_45_out, nand_47_out);
  nand nand_46 (nand_46_out, nor_26_out, nor_30_out, nor_34_out);
  nor nor_34 (nor_34_out, Instruction[5], d_ff_6_q);
  nor nor_35 (nor_35_out, not_7_out, d_ff_6_q);
  not not_7 (not_7_out, Instruction[4]);
  nor nor_36 (nor_36_out, nand_45_out, nand_48_out);
  nor nor_37 (nor_37_out, nand_45_out, nand_49_out);
  nand nand_47 (nand_47_out, nor_35_out, nor_39_out);
  nand nand_48 (nand_48_out, nor_35_out, nor_41_out);
  nor nor_38 (nor_38_out, Instruction[4], d_ff_6_q);
  nor nor_39 (nor_39_out, not_8_out, d_ff_6_q);
  not not_8 (not_8_out, Instruction[3]);
  nor nor_40 (nor_40_out, nand_45_out, nand_50_out);
  nand nand_49 (nand_49_out, nor_38_out, nor_39_out);
  nand nand_50 (nand_50_out, nor_38_out, nor_41_out);
  nor nor_41 (nor_41_out, Instruction[3], d_ff_6_q);
  nor nor_42 (nor_42_out, not_9_out, d_ff_6_q);
  not not_9 (not_9_out, Instruction[2]);
  nand nand_51 (nand_51_out, nor_42_out, nor_44_out, nor_48_out);
  nor nor_43 (nor_43_out, Instruction[2], d_ff_6_q);
  nor nor_44 (nor_44_out, not_10_out, d_ff_6_q);
  not not_10 (not_10_out, Instruction[1]);
  nor nor_45 (nor_45_out, nand_47_out, nand_46_out, nand_52_out);
  nor nor_46 (nor_46_out, nand_47_out, nand_46_out, nand_53_out);
  nand nand_52 (nand_52_out, nor_42_out, nor_44_out, nor_51_out);
  nand nand_53 (nand_53_out, nor_42_out, nor_47_out, nor_48_out);
  nor nor_47 (nor_47_out, Instruction[1], d_ff_6_q);
  nor nor_48 (nor_48_out, not_11_out, d_ff_6_q);
  not not_11 (not_11_out, Instruction[0]);
  nor nor_49 (nor_49_out, nand_47_out, nand_46_out, nand_54_out);
  nor nor_50 (nor_50_out, nand_47_out, nand_46_out, nand_55_out);
  nand nand_54 (nand_54_out, nor_42_out, nor_47_out, nor_51_out);
  nand nand_55 (nand_55_out, nor_43_out, nor_44_out, nor_48_out);
  nor nor_51 (nor_51_out, Instruction[0], d_ff_6_q);
  nor nor_52 (nor_52_out, nand_47_out, nand_46_out, nand_56_out);
  nor nor_53 (nor_53_out, nand_47_out, nand_46_out, nand_57_out);
  nand nand_56 (nand_56_out, nor_43_out, nor_44_out, nor_51_out);
  nand nand_57 (nand_57_out, nor_43_out, nor_47_out, nor_48_out);
  nor nor_54 (nor_54_out, nand_47_out, nand_46_out, nand_58_out);
  nand nand_58 (nand_58_out, nor_43_out, nor_47_out, nor_51_out);
  nor nor_55 (nor_55_out, nand_48_out, nand_46_out, nand_56_out);
  nor nor_56 (nor_56_out, nand_48_out, nand_46_out, nand_57_out);
  nor nor_57 (nor_57_out, nand_48_out, nand_46_out, nand_58_out);
  nor nor_58 (nor_58_out, nand_49_out, nand_46_out, nand_51_out);
  nor nor_59 (nor_59_out, nand_49_out, nand_46_out, nand_52_out);
  nor nor_60 (nor_60_out, nand_49_out, nand_46_out, nand_53_out);
  nor nor_61 (nor_61_out, nand_49_out, nand_46_out, nand_54_out);
  nor nor_62 (nor_62_out, nand_49_out, nand_46_out, nand_55_out);
  nor nor_63 (nor_63_out, nand_49_out, nand_46_out, nand_56_out);
  nor nor_64 (nor_64_out, nand_49_out, nand_46_out, nand_57_out);
  nor nor_65 (nor_65_out, nand_49_out, nand_46_out, nand_58_out);
  nor nor_66 (nor_66_out, nand_50_out, nand_46_out, nand_51_out);
  nor nor_67 (nor_67_out, nand_50_out, nand_46_out, nand_52_out);
  nor nor_68 (nor_68_out, nand_50_out, nand_46_out, nand_53_out);
  nor nor_69 (nor_69_out, nand_50_out, nand_46_out, nand_54_out);
  nor nor_70 (nor_70_out, nand_50_out, nand_46_out, nand_55_out);
  nor nor_71 (nor_71_out, nand_50_out, nand_46_out, nand_56_out);
  nor nor_72 (nor_72_out, nand_50_out, nand_46_out, nand_57_out);
  nor nor_73 (nor_73_out, nand_50_out, nand_46_out, nand_58_out);
  not not_12 (not_12_out, d_ff_6_q);
  nand nand_59 (nand_59_out, d_ff_1_q, not_12_out);
  not not_13 (IR_WE, nand_59_out);
  or or_4 (or_4_out, Flags_Out[1], d_ff_3_q, d_ff_2_q);
  or or_5 (or_5_out, d_ff_5_q, Flags_Out[1]);
  or or_6 (or_6_out, d_ff_3_q, d_ff_2_q);
  or or_7 (or_7_out, Flags_Out[1], d_ff_3_q);
  nand nand_60 (nand_60_out, d_ff_6_q, or_4_out);
  nand nand_61 (nand_61_out, or_4_out, nor_69_out);
  nand nand_62 (nand_62_out, or_5_out, nor_68_out);
  nand nand_63 (nand_63_out, or_6_out, nor_67_out);
  nand nand_64 (nand_64_out, d_ff_3_q, nor_66_out);
  nand nand_65 (nand_65_out, d_ff_2_q, nor_65_out);
  nand nand_66 (nand_66_out, or_6_out, nor_59_out);
  nand nand_67 (nand_67_out, or_7_out, nor_56_out);
  nand nand_68 (nand_68_out, d_ff_2_q, nor_33_out);
  nand nand_69 (nand_69_out, d_ff_3_q, nor_28_out);
  nand nand_70 (nand_70_out, nand_61_out, nand_62_out, nand_63_out);
  nand nand_71 (nand_71_out, nand_64_out, nand_65_out, nand_66_out);
  nand nand_72 (nand_72_out, nand_67_out, nand_68_out, nand_69_out);
  nor nor_74 (nor_74_out, nand_70_out, nand_71_out, nand_72_out);
  nand nand_73 (ADDR_SEL[0], nor_74_out, nand_60_out, nor_75_out);
  nand nand_74 (ADDR_SEL[1], nor_74_out, nand_60_out, and_4_out);
  nand nand_75 (nand_75_out, nand_77_out, nand_78_out, nand_79_out);
  nor nor_75 (nor_75_out, nand_75_out, nand_76_out);
  nand nand_76 (nand_76_out, nand_80_out, nand_81_out, nand_82_out);
  and and_4 (and_4_out, nand_83_out, nand_84_out);
  nand nand_77 (nand_77_out, nor_61_out, or_8_out);
  or or_8 (or_8_out, Flags_Out[1], d_ff_5_q);
  nand nand_78 (nand_78_out, nor_60_out, or_9_out);
  or or_9 (or_9_out, d_ff_2_q, d_ff_3_q);
  nand nand_79 (nand_79_out, nor_58_out, or_8_out);
  nand nand_80 (nand_80_out, nor_57_out, or_9_out);
  nand nand_81 (nand_81_out, nor_37_out, Flags_Out[1]);
  nand nand_82 (nand_82_out, nor_32_out, Flags_Out[1]);
  nand nand_83 (nand_83_out, nor_36_out, d_ff_2_q);
  nand nand_84 (nand_84_out, nor_29_out, d_ff_2_q);
  nand nand_85 (nand_85_out, d_ff_6_q, d_ff_1_q);
  D_Flip_Flop d_ff_6 (.D(INT_In), .clk(d_ff_1_q), .Q(d_ff_6_q), .reset(CLR));  // open: Qn, preset
  nand nand_86 (nand_86_out, nor_71_out, d_ff_2_q);
  nand nand_87 (nand_87_out, nor_70_out, d_ff_2_q);
  and and_5 (INT_WH, nor_72_out, d_ff_3_q);
  nand nand_88 (nand_88_out, nor_69_out, d_ff_2_q);
  and and_6 (INT_WL, nor_72_out, d_ff_2_q);
  nand nand_89 (INT_Enable, nand_88_out, nand_87_out);
  nand nand_90 (INT_Disable, nand_86_out, nand_85_out);

  assign out_27 = Instruction[7:4];

  // Notes on the sheet:
  //   Program Counter
endmodule
